// Logisim project projet.circ as structural Verilog
module main (
  output buzzer_0,
  output buzzer_1
);

  wire alarme_2_1_alarme, and_1_out, and_2_out, B_0_out, B_1_out, clock_1_out, clock_2_out, comparator_1_eq,
       debouncer_1_output_1, debouncer_2_output_1, dip_switch_sw1, dip_switch_sw2, dip_switch_sw3,
       dip_switch_sw4, dip_switch_sw5, dip_switch_sw6, dip_switch_sw7, dip_switch_sw8, dip_switch_sw9,
       dip_switch_sw10, jukebox_1_set_music_on, not_1_out, or_1_out, output_logic_1_a, output_logic_1_b,
       output_logic_1_c, output_logic_1_d, output_logic_1_e, output_logic_1_f, output_logic_1_g,
       output_logic_1_p, output_logic_2_a, output_logic_2_b, output_logic_2_c, output_logic_2_d,
       output_logic_2_e, output_logic_2_f, output_logic_2_g, output_logic_2_p, output_logic_3_a,
       output_logic_3_b, output_logic_3_c, output_logic_3_d, output_logic_3_e, output_logic_3_f,
       output_logic_3_g, output_logic_3_p, output_logic_4_a, output_logic_4_b, output_logic_4_c,
       output_logic_4_d, output_logic_4_e, output_logic_4_f, output_logic_4_g, output_logic_4_p,
       output_logic_5_a, output_logic_5_b, output_logic_5_c, output_logic_5_d, output_logic_5_e,
       output_logic_5_f, output_logic_5_g, output_logic_5_p, output_logic_6_a, output_logic_6_b,
       output_logic_6_c, output_logic_6_d, output_logic_6_e, output_logic_6_f, output_logic_6_g,
       output_logic_6_p, reset_mode_1_r, transition_logic_1_s_0, transition_logic_1_s_1,
       transition_logic_1_s_2, transition_logic_1_s_3;
  wire [1:0] jukebox_1_o_music;
  wire [3:0] d_ff_4_q;
  wire [4:0] multiplexer_2_out, multiplexer_3_out, multiplexer_4_out, multiplexer_5_out, multiplexer_6_out,
       multiplexer_7_out;
  wire [11:0] demultiplexer_1_out3, demultiplexer_1_out5, demultiplexer_1_out7, demultiplexer_1_out9,
       demultiplexer_1_out11, transition_logic_1_input_bus;
  wire [29:0] alarme_2_1_o_0, chrono_1_o_0, jukebox_1_o_text, memory_time_1_o_0, multiplexer_1_out,
       set_time_setter_1_o_0, set_time_zone_1_o_text, set_time_zone_1_o_time;

  Button B_1 (.out(B_1_out));
  Button B_0 (.out(B_0_out));
  to_one_tic debouncer_1 (.I_0(B_1_out), .R(reset_mode_1_r), .Output_1(debouncer_1_output_1));
  to_one_tic debouncer_2 (.I_0(B_0_out), .R(reset_mode_1_r), .Output_1(debouncer_2_output_1));
  not not_1 (not_1_out, reset_mode_1_r);
  DipSwitch #(.number(10)) dip_switch (
    .sw1(dip_switch_sw1), .sw2(dip_switch_sw2), .sw3(dip_switch_sw3), .sw4(dip_switch_sw4),
    .sw5(dip_switch_sw5), .sw6(dip_switch_sw6), .sw7(dip_switch_sw7), .sw8(dip_switch_sw8),
    .sw9(dip_switch_sw9), .sw10(dip_switch_sw10));
  and and_1 (and_1_out, not_1_out, debouncer_1_output_1);
  and and_2 (and_2_out, debouncer_2_output_1, not_1_out);
  or or_1 (or_1_out, alarme_2_1_alarme, jukebox_1_set_music_on);
  reset_mode reset_mode_1 (.B_1(B_1_out), .B_0(B_0_out), .R(reset_mode_1_r));
  musique musique_1 (.set_on(or_1_out), .music(jukebox_1_o_music), .buzzer_0(buzzer_0), .buzzer_1(buzzer_1));
  transition_logic transition_logic_1 (
    .C_3(d_ff_4_q[3]), .C_2(d_ff_4_q[2]), .C_1(d_ff_4_q[1]), .C_0(d_ff_4_q[0]), .B_1(and_1_out),
    .B_0(and_2_out), .DS_9(dip_switch_sw10), .DS_8(dip_switch_sw9), .DS_7(dip_switch_sw8),
    .DS_6(dip_switch_sw7), .DS_5(dip_switch_sw6), .DS_4(dip_switch_sw5), .DS_3(dip_switch_sw4),
    .DS_2(dip_switch_sw3), .DS_1(dip_switch_sw2), .DS_0(dip_switch_sw1), .S_3(transition_logic_1_s_3),
    .S_2(transition_logic_1_s_2), .S_1(transition_logic_1_s_1), .S_0(transition_logic_1_s_0),
    .input_bus(transition_logic_1_input_bus));
  Clock clock_1 (.out(clock_1_out));
  D_Flip_Flop d_ff_1 (
    .D(transition_logic_1_s_3), .clk(clock_1_out), .Q(d_ff_4_q[3]), .reset(reset_mode_1_r));  // open: Qn, preset
  D_Flip_Flop d_ff_2 (
    .D(transition_logic_1_s_2), .clk(clock_1_out), .Q(d_ff_4_q[2]), .reset(reset_mode_1_r));  // open: Qn, preset
  D_Flip_Flop d_ff_3 (
    .D(transition_logic_1_s_1), .clk(clock_1_out), .Q(d_ff_4_q[1]), .reset(reset_mode_1_r));  // open: Qn, preset
  D_Flip_Flop d_ff_4 (
    .D(transition_logic_1_s_0), .clk(clock_1_out), .Q(d_ff_4_q[0]), .reset(reset_mode_1_r));  // open: Qn, preset
  Demultiplexer #(.select(4), .width(12), .enable("false")) demultiplexer_1 (
    .out3(demultiplexer_1_out3), .out5(demultiplexer_1_out5), .out7(demultiplexer_1_out7),
    .out9(demultiplexer_1_out9), .out11(demultiplexer_1_out11), .in(transition_logic_1_input_bus),
    .sel(d_ff_4_q));  // open: out0, out1, out2, out4, out6, out8, out10, out12, out13, out14, out15
  Clock #(.highDuration(1000000), .lowDuration(1000000)) clock_2 (.out(clock_2_out));
  Comparator #(.width(4)) comparator_1 (.a(d_ff_4_q), .b(4'b0011), .eq(comparator_1_eq));  // open: gt, lt
  // Probe on memory_time_1_o_0
  Multiplexer #(.select(4), .width(30), .enable("false")) multiplexer_1 (
    .in0({30{1'b0}}), .in1({30{1'b0}}), .in2({30{1'b0}}), .in3(set_time_setter_1_o_0), .in4({30{1'b0}}),
    .in5({30{1'b0}}), .in6({30{1'b0}}), .in7(set_time_zone_1_o_time), .in8({30{1'b0}}), .in9({30{1'b0}}),
    .in10({30{1'b0}}), .in11({30{1'b0}}), .in12({30{1'b0}}), .in13({30{1'b0}}), .in14({30{1'b0}}),
    .in15({30{1'b0}}), .out(multiplexer_1_out), .sel(d_ff_4_q));
  // Probe on set_time_zone_1_o_time[29:25]
  // Probe on set_time_zone_1_o_time[24:20]
  // Probe on set_time_zone_1_o_time[19:15]
  // Probe on set_time_zone_1_o_time[14:10]
  // Probe on set_time_zone_1_o_time[9:5]
  // Probe on set_time_zone_1_o_time[4:0]
  memory_time memory_time_1 (
    .I_0(multiplexer_1_out), .clock_in(clock_2_out), .reset(reset_mode_1_r), .load(d_ff_4_q),
    .O_0(memory_time_1_o_0));  // open: carry
  set_time_setter set_time_setter_1 (
    .I_0(memory_time_1_o_0), .input_bus(demultiplexer_1_out3), .mode_on(comparator_1_eq), .R(reset_mode_1_r),
    .O_0(set_time_setter_1_o_0));
  alarme_2 alarme_2_1 (
    .time_bus(memory_time_1_o_0), .input_bus(demultiplexer_1_out5), .mode_on(d_ff_4_q),
    .B_1(debouncer_1_output_1), .B_0(debouncer_2_output_1), .R(reset_mode_1_r), .alarme(alarme_2_1_alarme),
    .O_0(alarme_2_1_o_0));
  set_time_zone set_time_zone_1 (
    .time_bus(memory_time_1_o_0), .mode_on(d_ff_4_q), .input_bus(demultiplexer_1_out7), .R(reset_mode_1_r),
    .O_text(set_time_zone_1_o_text), .O_time(set_time_zone_1_o_time));
  // Probe on set_time_zone_1_o_time
  jukebox jukebox_1 (
    .mode_on(d_ff_4_q), .input_bus(demultiplexer_1_out9), .R(reset_mode_1_r), .O_text(jukebox_1_o_text),
    .O_music(jukebox_1_o_music), .set_music_on(jukebox_1_set_music_on));
  chrono chrono_1 (.input_bus(demultiplexer_1_out11), .mode_on(d_ff_4_q), .R(reset_mode_1_r), .O_0(chrono_1_o_0));
  Multiplexer #(.select(4), .width(5), .enable("false")) multiplexer_2 (
    .in0(memory_time_1_o_0[29:25]), .in1(5'b11101), .in2(5'b11100), .in3(set_time_setter_1_o_0[29:25]),
    .in4(5'b11100), .in5(alarme_2_1_o_0[29:25]), .in6(5'b11011), .in7(set_time_zone_1_o_text[29:25]),
    .in8(5'b10011), .in9(jukebox_1_o_text[29:25]), .in10(5'b01100), .in11(chrono_1_o_0[29:25]),
    .out(multiplexer_2_out), .sel(d_ff_4_q));  // open: in12, in13, in14, in15
  Multiplexer #(.select(4), .width(5), .enable("false")) multiplexer_3 (
    .in0(memory_time_1_o_0[24:20]), .in1(5'b10010), .in2(5'b01110), .in3(set_time_setter_1_o_0[24:20]),
    .in4(5'b01110), .in5(alarme_2_1_o_0[24:20]), .in6(5'b01110), .in7(set_time_zone_1_o_text[24:20]),
    .in8(5'b11110), .in9(jukebox_1_o_text[24:20]), .in10(5'b10001), .in11(chrono_1_o_0[24:20]),
    .out(multiplexer_3_out), .sel(d_ff_4_q));  // open: in12, in13, in14, in15
  Multiplexer #(.select(4), .width(5), .enable("false")) multiplexer_4 (
    .in0(memory_time_1_o_0[19:15]), .in1(5'b11110), .in2(5'b11101), .in3(set_time_setter_1_o_0[19:15]),
    .in4(5'b11101), .in5(alarme_2_1_o_0[19:15]), .in6(5'b10000), .in7(set_time_zone_1_o_text[19:15]),
    .in8(5'b10100), .in9(jukebox_1_o_text[19:15]), .in10(5'b11011), .in11(chrono_1_o_0[19:15]),
    .out(multiplexer_4_out), .sel(d_ff_4_q));  // open: in12, in13, in14, in15
  Multiplexer #(.select(4), .width(5), .enable("false")) multiplexer_5 (
    .in0(memory_time_1_o_0[14:10]), .in1(5'b01110), .in2({5{1'b1}}), .in3(set_time_setter_1_o_0[14:10]),
    .in4({5{1'b1}}), .in5(alarme_2_1_o_0[14:10]), .in6(5'b10010), .in7(set_time_zone_1_o_text[14:10]),
    .in8(5'b01110), .in9(jukebox_1_o_text[14:10]), .in10(5'b11000), .in11(chrono_1_o_0[14:10]),
    .out(multiplexer_5_out), .sel(d_ff_4_q));  // open: in12, in13, in14, in15
  Multiplexer #(.select(4), .width(5), .enable("false")) multiplexer_6 (
    .in0(memory_time_1_o_0[9:5]), .in1({5{1'b1}}), .in2(5'b11101), .in3(set_time_setter_1_o_0[9:5]),
    .in4(5'b01010), .in5(alarme_2_1_o_0[9:5]), .in6(5'b11000), .in7(set_time_zone_1_o_text[9:5]),
    .in8(5'b01011), .in9(jukebox_1_o_text[9:5]), .in10(5'b10111), .in11(chrono_1_o_0[9:5]),
    .out(multiplexer_6_out), .sel(d_ff_4_q));  // open: in12, in13, in14, in15
  Multiplexer #(.select(4), .width(5), .enable("false")) multiplexer_7 (
    .in0(memory_time_1_o_0[4:0]), .in1({5{1'b1}}), .in2({5{1'b1}}), .in3(set_time_setter_1_o_0[4:0]),
    .in4({5{1'b1}}), .in5(alarme_2_1_o_0[4:0]), .in6(5'b10111), .in7(set_time_zone_1_o_text[4:0]),
    .in8(5'b11000), .in9(jukebox_1_o_text[4:0]), .in10(5'b11000), .in11(chrono_1_o_0[4:0]),
    .out(multiplexer_7_out), .sel(d_ff_4_q));  // open: in12, in13, in14, in15
  LED LED_1 (.in(1'b0));
  LED LED_2 (.in(1'b0));
  LED LED_3 (.in(1'b0));
  LED LED_4 (.in(1'b0));
  LED LED_5 (.in(1'b0));
  LED LED_6 (.in(1'b0));
  LED LED_7 (.in(1'b0));
  LED LED_8 (.in(1'b0));
  LED LED_9 (.in(1'b0));
  LED LED_10 (.in(1'b0));
  output_logic output_logic_1 (
    .I(multiplexer_2_out), .a(output_logic_1_a), .b(output_logic_1_b), .c(output_logic_1_c),
    .d(output_logic_1_d), .e(output_logic_1_e), .f(output_logic_1_f), .g(output_logic_1_g),
    .p(output_logic_1_p));  // open: point
  output_logic output_logic_2 (
    .I(multiplexer_3_out), .a(output_logic_2_a), .b(output_logic_2_b), .c(output_logic_2_c),
    .d(output_logic_2_d), .e(output_logic_2_e), .f(output_logic_2_f), .g(output_logic_2_g),
    .p(output_logic_2_p));  // open: point
  output_logic output_logic_3 (
    .I(multiplexer_4_out), .a(output_logic_3_a), .b(output_logic_3_b), .c(output_logic_3_c),
    .d(output_logic_3_d), .e(output_logic_3_e), .f(output_logic_3_f), .g(output_logic_3_g),
    .p(output_logic_3_p));  // open: point
  output_logic output_logic_4 (
    .I(multiplexer_5_out), .a(output_logic_4_a), .b(output_logic_4_b), .c(output_logic_4_c),
    .d(output_logic_4_d), .e(output_logic_4_e), .f(output_logic_4_f), .g(output_logic_4_g),
    .p(output_logic_4_p));  // open: point
  output_logic output_logic_5 (
    .I(multiplexer_6_out), .a(output_logic_5_a), .b(output_logic_5_b), .c(output_logic_5_c),
    .d(output_logic_5_d), .e(output_logic_5_e), .f(output_logic_5_f), .g(output_logic_5_g),
    .p(output_logic_5_p));  // open: point
  output_logic output_logic_6 (
    .I(multiplexer_7_out), .a(output_logic_6_a), .b(output_logic_6_b), .c(output_logic_6_c),
    .d(output_logic_6_d), .e(output_logic_6_e), .f(output_logic_6_f), .g(output_logic_6_g),
    .p(output_logic_6_p));  // open: point
  _7_Segment_Display L_7_Segment_Display_1 (
    .g(output_logic_1_g), .f(output_logic_1_f), .a(output_logic_1_a), .b(output_logic_1_b),
    .e(output_logic_1_e), .d(output_logic_1_d), .c(output_logic_1_c), .dp(output_logic_1_p));
  _7_Segment_Display L_7_Segment_Display_2 (
    .g(output_logic_2_g), .f(output_logic_2_f), .a(output_logic_2_a), .b(output_logic_2_b),
    .e(output_logic_2_e), .d(output_logic_2_d), .c(output_logic_2_c), .dp(output_logic_2_p));
  _7_Segment_Display L_7_Segment_Display_3 (
    .g(output_logic_3_g), .f(output_logic_3_f), .a(output_logic_3_a), .b(output_logic_3_b),
    .e(output_logic_3_e), .d(output_logic_3_d), .c(output_logic_3_c), .dp(output_logic_3_p));
  _7_Segment_Display L_7_Segment_Display_4 (
    .g(output_logic_4_g), .f(output_logic_4_f), .a(output_logic_4_a), .b(output_logic_4_b),
    .e(output_logic_4_e), .d(output_logic_4_d), .c(output_logic_4_c), .dp(output_logic_4_p));
  _7_Segment_Display L_7_Segment_Display_5 (
    .g(output_logic_5_g), .f(output_logic_5_f), .a(output_logic_5_a), .b(output_logic_5_b),
    .e(output_logic_5_e), .d(output_logic_5_d), .c(output_logic_5_c), .dp(output_logic_5_p));
  _7_Segment_Display L_7_Segment_Display_6 (
    .g(output_logic_6_g), .f(output_logic_6_f), .a(output_logic_6_a), .b(output_logic_6_b),
    .e(output_logic_6_e), .d(output_logic_6_d), .c(output_logic_6_c), .dp(output_logic_6_p));
endmodule

module output_logic (
  input  point,
  input  [4:0] I,
  output a,
  output b,
  output c,
  output d,
  output e,
  output f,
  output g,
  output p
);

  wire and_1_out, and_2_out, and_3_out, and_4_out, and_5_out, and_6_out, and_7_out, and_8_out, and_9_out,
       and_10_out, and_11_out, and_12_out, and_13_out, and_14_out, and_15_out, and_16_out, and_17_out,
       and_18_out, and_19_out, and_20_out, and_21_out, and_22_out, and_23_out, and_24_out, and_25_out,
       and_26_out, and_27_out, and_28_out, and_29_out, and_30_out, and_31_out, and_32_out, and_33_out,
       and_34_out, and_35_out, and_36_out, and_37_out, and_38_out, and_39_out, and_40_out, and_41_out,
       and_42_out, and_43_out, and_44_out, and_45_out, and_46_out, and_47_out, and_48_out, and_49_out,
       and_50_out, and_51_out, and_52_out, and_53_out, and_54_out, and_55_out, and_56_out, and_57_out,
       and_58_out, not_1_out, not_2_out, not_3_out, not_4_out, not_5_out, not_6_out, not_7_out, not_8_out,
       not_9_out, not_10_out, not_11_out, not_12_out, not_13_out, not_14_out, not_15_out, not_16_out,
       not_17_out, not_18_out, not_19_out, not_20_out, not_21_out, not_22_out, not_23_out, not_24_out,
       not_25_out, not_26_out, not_27_out, not_28_out, not_29_out, not_30_out, not_31_out, not_32_out,
       not_33_out, not_34_out, not_35_out, not_36_out, not_37_out, not_38_out, not_39_out, not_40_out,
       not_41_out, not_42_out, not_43_out, not_44_out, not_45_out, not_46_out, not_47_out, not_48_out,
       not_49_out, not_50_out, not_51_out, not_52_out, not_53_out, not_54_out, not_55_out, not_56_out,
       not_57_out, not_58_out, not_59_out, not_60_out, not_61_out, not_62_out, not_63_out, not_64_out,
       not_65_out, not_66_out, not_67_out, not_68_out, not_69_out, not_70_out, not_71_out, not_72_out,
       not_73_out, not_74_out, not_75_out, not_76_out, not_77_out, not_78_out, not_79_out, not_80_out,
       not_81_out, not_82_out, not_83_out, not_84_out, not_85_out, not_86_out, not_87_out, not_88_out,
       not_89_out, not_90_out, not_91_out, not_92_out, not_93_out, not_94_out, not_95_out, not_96_out,
       not_97_out, not_98_out, not_99_out, not_100_out, not_101_out, not_102_out;

  not not_1 (not_1_out, I[4]);
  not not_2 (not_2_out, I[2]);
  not not_3 (not_3_out, I[0]);
  not not_4 (not_4_out, I[4]);
  not not_5 (not_5_out, I[3]);
  not not_6 (not_6_out, I[4]);
  not not_7 (not_7_out, I[3]);
  not not_8 (not_8_out, I[4]);
  not not_9 (not_9_out, I[4]);
  not not_10 (not_10_out, I[0]);
  not not_11 (not_11_out, I[2]);
  not not_12 (not_12_out, I[1]);
  not not_13 (not_13_out, I[2]);
  not not_14 (not_14_out, I[0]);
  not not_15 (not_15_out, I[1]);
  not not_16 (not_16_out, I[0]);
  not not_17 (not_17_out, I[3]);
  not not_18 (not_18_out, I[0]);
  not not_19 (not_19_out, I[4]);
  not not_20 (not_20_out, I[3]);
  not not_21 (not_21_out, I[1]);
  not not_22 (not_22_out, I[0]);
  not not_23 (not_23_out, I[4]);
  not not_24 (not_24_out, I[2]);
  not not_25 (not_25_out, I[0]);
  not not_26 (not_26_out, I[3]);
  not not_27 (not_27_out, I[2]);
  not not_28 (not_28_out, I[3]);
  not not_29 (not_29_out, I[2]);
  not not_30 (not_30_out, I[4]);
  not not_31 (not_31_out, I[3]);
  not not_32 (not_32_out, I[2]);
  not not_33 (not_33_out, I[1]);
  not not_34 (not_34_out, I[4]);
  not not_35 (not_35_out, I[1]);
  not not_36 (not_36_out, I[0]);
  not not_37 (not_37_out, I[4]);
  not not_38 (not_38_out, I[3]);
  not not_39 (not_39_out, I[1]);
  not not_40 (not_40_out, I[3]);
  not not_41 (not_41_out, I[2]);
  not not_42 (not_42_out, I[1]);
  not not_43 (not_43_out, I[4]);
  not not_44 (not_44_out, I[1]);
  not not_45 (not_45_out, I[3]);
  not not_46 (not_46_out, I[4]);
  not not_47 (not_47_out, I[3]);
  not not_48 (not_48_out, I[4]);
  not not_49 (not_49_out, I[2]);
  not not_50 (not_50_out, I[0]);
  not not_51 (not_51_out, I[2]);
  not not_52 (not_52_out, I[1]);
  not not_53 (not_53_out, I[0]);
  not not_54 (not_54_out, I[4]);
  not not_55 (not_55_out, I[3]);
  not not_56 (not_56_out, I[0]);
  not not_57 (not_57_out, I[3]);
  not not_58 (not_58_out, I[2]);
  not not_59 (not_59_out, I[1]);
  not not_60 (not_60_out, I[4]);
  not not_61 (not_61_out, I[2]);
  not not_62 (not_62_out, I[0]);
  not not_63 (not_63_out, I[4]);
  not not_64 (not_64_out, I[2]);
  not not_65 (not_65_out, I[0]);
  not not_66 (not_66_out, I[0]);
  not not_67 (not_67_out, I[2]);
  not not_68 (not_68_out, I[4]);
  not not_69 (not_69_out, I[2]);
  not not_70 (not_70_out, I[1]);
  not not_71 (not_71_out, I[1]);
  not not_72 (not_72_out, I[3]);
  not not_73 (not_73_out, I[1]);
  not not_74 (not_74_out, I[0]);
  not not_75 (not_75_out, I[4]);
  not not_76 (not_76_out, I[0]);
  not not_77 (not_77_out, I[3]);
  not not_78 (not_78_out, I[1]);
  not not_79 (not_79_out, I[2]);
  not not_80 (not_80_out, I[1]);
  not not_81 (not_81_out, I[0]);
  not not_82 (not_82_out, I[4]);
  not not_83 (not_83_out, I[1]);
  not not_84 (not_84_out, I[4]);
  not not_85 (not_85_out, I[2]);
  not not_86 (not_86_out, I[4]);
  not not_87 (not_87_out, I[1]);
  not not_88 (not_88_out, I[4]);
  not not_89 (not_89_out, I[0]);
  not not_90 (not_90_out, I[1]);
  not not_91 (not_91_out, I[0]);
  not not_92 (not_92_out, I[4]);
  not not_93 (not_93_out, I[2]);
  not not_94 (not_94_out, I[1]);
  not not_95 (not_95_out, I[2]);
  not not_96 (not_96_out, I[1]);
  not not_97 (not_97_out, I[3]);
  not not_98 (not_98_out, I[4]);
  not not_99 (not_99_out, I[3]);
  not not_100 (not_100_out, I[2]);
  not not_101 (not_101_out, I[1]);
  not not_102 (not_102_out, I[0]);
  and and_1 (and_1_out, not_1_out, not_2_out, not_3_out);
  and and_2 (and_2_out, not_4_out, not_5_out, I[1]);
  and and_3 (and_3_out, not_6_out, not_7_out, I[2], I[0]);
  and and_4 (and_4_out, not_8_out, I[2], I[1]);
  and and_5 (and_5_out, not_9_out, I[3], not_10_out);
  and and_6 (and_6_out, I[3], not_11_out, not_12_out);
  and and_7 (and_7_out, I[3], not_13_out, not_14_out);
  and and_8 (and_8_out, I[4], not_15_out, not_16_out);
  and and_9 (and_9_out, I[4], not_17_out, I[2], not_18_out);
  and and_10 (and_10_out, not_19_out, not_20_out, not_21_out, not_22_out);
  and and_11 (and_11_out, not_23_out, not_24_out, not_25_out);
  and and_12 (and_12_out, not_26_out, not_27_out, I[0]);
  and and_13 (and_13_out, not_28_out, not_29_out, I[1]);
  and and_14 (and_14_out, not_30_out, not_31_out, I[1], I[0]);
  and and_15 (and_15_out, I[3], not_32_out, not_33_out);
  and and_16 (and_16_out, not_34_out, I[3], not_35_out, I[0]);
  and and_17 (and_17_out, I[4], I[3], I[1], not_36_out);
  and and_18 (and_18_out, not_37_out, not_38_out, not_39_out);
  and and_19 (and_19_out, not_40_out, not_41_out, not_42_out);
  and and_20 (and_20_out, not_43_out, not_44_out, I[0]);
  and and_21 (and_21_out, not_45_out, I[1], I[0]);
  and and_22 (and_22_out, not_46_out, not_47_out, I[2]);
  and and_23 (and_23_out, not_48_out, I[3], not_49_out);
  and and_24 (and_24_out, I[4], not_50_out);
  and and_25 (and_25_out, not_51_out, not_52_out, not_53_out);
  and and_26 (and_26_out, not_54_out, not_55_out, I[1], not_56_out);
  and and_27 (and_27_out, not_57_out, not_58_out, I[1], I[0]);
  and and_28 (and_28_out, I[2], not_59_out, I[0]);
  and and_29 (and_29_out, not_60_out, I[3], not_61_out, I[0]);
  and and_30 (and_30_out, I[3], I[2], not_62_out);
  and and_31 (and_31_out, not_63_out, not_64_out, not_65_out);
  and and_32 (and_32_out, I[2], I[1], not_66_out);
  and and_33 (and_33_out, I[3], not_67_out, I[1], I[0]);
  and and_34 (and_34_out, not_68_out, I[3], I[2]);
  and and_35 (and_35_out, I[4], not_69_out, not_70_out);
  and and_36 (and_36_out, I[4], not_71_out, I[0]);
  and and_37 (and_37_out, I[4], not_72_out, I[2]);
  and and_38 (and_38_out, not_73_out, not_74_out);
  and and_39 (and_39_out, not_75_out, I[2], not_76_out);
  and and_40 (and_40_out, not_77_out, I[2], not_78_out);
  and and_41 (and_41_out, I[3], not_79_out, not_80_out);
  and and_42 (and_42_out, I[3], not_81_out);
  and and_43 (and_43_out, not_82_out, I[3], I[1]);
  and and_44 (and_44_out, I[4], not_83_out);
  and and_45 (and_45_out, not_84_out, not_85_out, I[1]);
  and and_46 (and_46_out, not_86_out, I[2], not_87_out);
  and and_47 (and_47_out, not_88_out, I[2], not_89_out);
  and and_48 (and_48_out, I[2], not_90_out, not_91_out);
  and and_49 (and_49_out, not_92_out, I[3]);
  and and_50 (and_50_out, I[3], not_93_out, I[1]);
  and and_51 (and_51_out, I[3], I[2], not_94_out);
  and and_52 (and_52_out, I[4], not_95_out, not_96_out, I[0]);
  and and_53 (and_53_out, I[4], not_97_out, I[2], I[1], I[0]);
  and and_54 (and_54_out, point, not_98_out);
  and and_55 (and_55_out, point, not_99_out);
  and and_56 (and_56_out, point, not_100_out);
  and and_57 (and_57_out, point, not_101_out);
  and and_58 (and_58_out, point, not_102_out);
  or or_1 (a, and_1_out, and_2_out, and_3_out, and_4_out, and_5_out, and_6_out, and_7_out, and_8_out, and_9_out);
  or or_2 (b, and_10_out, and_11_out, and_12_out, and_13_out, and_14_out, and_15_out, and_16_out, and_17_out);
  or or_3 (c, and_18_out, and_19_out, and_20_out, and_21_out, and_22_out, and_23_out, and_24_out);
  or or_4 (d, and_25_out, and_26_out, and_27_out, and_28_out, and_29_out, and_30_out);
  or or_5 (e, and_31_out, and_32_out, and_33_out, and_34_out, and_35_out, and_36_out, and_37_out);
  or or_6 (f, and_38_out, and_39_out, and_40_out, and_41_out, and_42_out, and_43_out, and_44_out);
  or or_7 (g, and_45_out, and_46_out, and_47_out, and_48_out, and_49_out, and_50_out, and_51_out, and_52_out, and_53_out);
  or or_8 (p, and_54_out, and_55_out, and_56_out, and_57_out, and_58_out);
endmodule

module transition_logic (
  input  C_3,
  input  C_2,
  input  C_1,
  input  C_0,
  input  B_1,
  input  B_0,
  input  DS_9,
  input  DS_8,
  input  DS_7,
  input  DS_6,
  input  DS_5,
  input  DS_4,
  input  DS_3,
  input  DS_2,
  input  DS_1,
  input  DS_0,
  output S_3,
  output S_2,
  output S_1,
  output S_0,
  output [11:0] input_bus
);

  wire in_impeach_1_o_0, in_impeach_1_o_1;

  in_impeach in_impeach_1 (
    .B_1(B_1), .B_0(B_0), .DS_9(DS_9), .DS_8(DS_8), .DS_7(DS_7), .DS_6(DS_6), .DS_5(DS_5), .DS_4(DS_4),
    .DS_3(DS_3), .DS_2(DS_2), .DS_1(DS_1), .DS_0(DS_0), .O_1(in_impeach_1_o_1), .O_0(in_impeach_1_o_0));
  transition_logic_half transition_logic_half_1 (
    .C_3(C_3), .C_2(C_2), .C_1(C_1), .C_0(C_0), .B_1(in_impeach_1_o_1), .B_0(in_impeach_1_o_0), .S_3(S_3),
    .S_2(S_2), .S_1(S_1), .S_0(S_0));

  assign input_bus = {B_1, B_0, DS_9, DS_8, DS_7, DS_6, DS_5, DS_4, DS_3, DS_2, DS_1, DS_0};
endmodule

module transition_logic_half (
  input  C_3,
  input  C_2,
  input  C_1,
  input  C_0,
  input  B_1,
  input  B_0,
  output S_3,
  output S_2,
  output S_1,
  output S_0
);

  wire and_1_out, and_2_out, and_3_out, and_4_out, and_5_out, and_6_out, and_7_out, and_8_out, and_9_out,
       and_10_out, and_11_out, and_12_out, and_13_out, and_14_out, and_15_out, and_16_out, and_17_out,
       and_18_out, and_19_out, and_20_out, and_21_out, and_22_out, and_23_out, and_24_out, and_25_out,
       and_26_out, and_27_out, not_1_out, not_2_out, not_3_out, not_4_out, not_5_out, not_6_out, not_7_out,
       not_8_out, not_9_out, not_10_out, not_11_out, not_12_out, not_13_out, not_14_out, not_15_out,
       not_16_out, not_17_out, not_18_out, not_19_out, not_20_out, not_21_out, not_22_out, not_23_out,
       not_24_out, not_25_out, not_26_out, not_27_out, not_28_out, not_29_out, not_30_out, not_31_out,
       not_32_out, not_33_out, not_34_out, not_35_out, not_36_out, not_37_out, not_38_out, not_39_out,
       not_40_out, not_41_out;

  not not_1 (not_1_out, C_3);
  not not_2 (not_2_out, C_0);
  not not_3 (not_3_out, B_0);
  not not_4 (not_4_out, C_2);
  not not_5 (not_5_out, C_1);
  not not_6 (not_6_out, C_2);
  not not_7 (not_7_out, B_1);
  not not_8 (not_8_out, C_2);
  not not_9 (not_9_out, C_2);
  not not_10 (not_10_out, C_3);
  not not_11 (not_11_out, C_2);
  not not_12 (not_12_out, C_0);
  not not_13 (not_13_out, B_0);
  not not_14 (not_14_out, C_1);
  not not_15 (not_15_out, B_1);
  not not_16 (not_16_out, B_0);
  not not_17 (not_17_out, C_3);
  not not_18 (not_18_out, C_3);
  not not_19 (not_19_out, C_2);
  not not_20 (not_20_out, B_0);
  not not_21 (not_21_out, C_3);
  not not_22 (not_22_out, B_1);
  not not_23 (not_23_out, C_2);
  not not_24 (not_24_out, B_1);
  not not_25 (not_25_out, B_1);
  not not_26 (not_26_out, B_0);
  not not_27 (not_27_out, C_1);
  not not_28 (not_28_out, C_0);
  not not_29 (not_29_out, B_0);
  not not_30 (not_30_out, C_1);
  not not_31 (not_31_out, C_0);
  not not_32 (not_32_out, B_0);
  not not_33 (not_33_out, B_0);
  not not_34 (not_34_out, C_0);
  not not_35 (not_35_out, B_1);
  not not_36 (not_36_out, B_1);
  not not_37 (not_37_out, B_0);
  not not_38 (not_38_out, B_0);
  not not_39 (not_39_out, B_0);
  not not_40 (not_40_out, B_0);
  not not_41 (not_41_out, B_0);
  and and_1 (and_1_out, not_1_out, C_2, C_1, not_2_out, B_1, not_3_out);
  and and_2 (and_2_out, C_3, not_4_out, not_5_out);
  and and_3 (and_3_out, C_3, not_6_out, not_7_out);
  and and_4 (and_4_out, C_3, not_8_out, B_0);
  and and_5 (and_5_out, C_3, not_9_out, C_0);
  and and_6 (and_6_out, not_10_out, not_11_out, C_1, not_12_out, B_1, not_13_out);
  and and_7 (and_7_out, C_2, not_14_out);
  and and_8 (and_8_out, C_2, not_15_out, not_16_out);
  and and_9 (and_9_out, not_17_out, C_2, B_0);
  and and_10 (and_10_out, C_2, C_0);
  and and_11 (and_11_out, C_3, C_2, B_1);
  and and_12 (and_12_out, not_18_out, not_19_out, C_0, B_1, not_20_out);
  and and_13 (and_13_out, not_21_out, C_1, not_22_out);
  and and_14 (and_14_out, not_23_out, C_1, not_24_out);
  and and_15 (and_15_out, C_1, not_25_out, not_26_out);
  and and_16 (and_16_out, C_1, B_1, B_0);
  and and_17 (and_17_out, C_1, C_0);
  and and_18 (and_18_out, C_2, not_27_out, not_28_out, B_1, not_29_out);
  and and_19 (and_19_out, C_3, not_30_out, not_31_out, B_1, not_32_out);
  and and_20 (and_20_out, C_3, C_2, C_1, not_33_out);
  and and_21 (and_21_out, not_34_out, not_35_out, B_0);
  and and_22 (and_22_out, C_0, not_36_out, not_37_out);
  and and_23 (and_23_out, C_0, B_1, B_0);
  and and_24 (and_24_out, C_1, C_0, not_38_out);
  and and_25 (and_25_out, C_2, C_0, not_39_out);
  and and_26 (and_26_out, C_3, C_0, not_40_out);
  and and_27 (and_27_out, C_3, C_1, B_1, not_41_out);
  or or_1 (S_3, and_1_out, and_2_out, and_3_out, and_4_out, and_5_out);
  or or_2 (S_2, and_6_out, and_7_out, and_8_out, and_9_out, and_10_out, and_11_out);
  or or_3 (S_1, and_12_out, and_13_out, and_14_out, and_15_out, and_16_out, and_17_out, and_18_out, and_19_out, and_20_out);
  or or_4 (S_0, and_21_out, and_22_out, and_23_out, and_24_out, and_25_out, and_26_out, and_27_out);
endmodule

module in_impeach (
  input  B_1,
  input  B_0,
  input  DS_9,
  input  DS_8,
  input  DS_7,
  input  DS_6,
  input  DS_5,
  input  DS_4,
  input  DS_3,
  input  DS_2,
  input  DS_1,
  input  DS_0,
  output O_1,
  output O_0
);

  wire nand_1_out, nand_2_out, nand_3_out, nand_4_out, nand_5_out, nand_6_out, nand_7_out, nand_8_out,
       nand_9_out, nand_10_out, nand_11_out, nand_12_out, nand_13_out, nand_14_out, nand_15_out, nand_16_out,
       nand_17_out, nand_18_out, nand_19_out, nand_20_out, nand_21_out, nand_22_out, nand_23_out,
       nand_24_out, nand_25_out, nand_26_out, nand_27_out, nand_28_out, nand_29_out, nand_30_out,
       nand_31_out, nand_32_out, nand_33_out, nand_34_out, nand_35_out, nand_36_out, nand_37_out,
       nand_38_out, nand_39_out, nand_40_out, nand_41_out, nand_42_out, nand_43_out, nand_44_out,
       nand_45_out, nand_46_out, nand_47_out, nand_48_out, nand_49_out, nand_50_out, nand_51_out,
       nand_52_out, nand_53_out, nand_54_out, nand_55_out, nand_56_out, nand_57_out, nand_58_out;

  nand nand_1 (nand_1_out, DS_0, DS_0);
  nand nand_2 (nand_2_out, DS_1, DS_1);
  nand nand_3 (nand_3_out, DS_3, DS_3);
  nand nand_4 (nand_4_out, DS_4, DS_4);
  nand nand_5 (nand_5_out, DS_6, DS_6);
  nand nand_6 (nand_6_out, DS_7, DS_7);
  nand nand_7 (nand_7_out, DS_0, DS_0);
  nand nand_8 (nand_8_out, DS_1, DS_1);
  nand nand_9 (nand_9_out, DS_3, DS_3);
  nand nand_10 (nand_10_out, DS_4, DS_4);
  nand nand_11 (nand_11_out, DS_6, DS_6);
  nand nand_12 (nand_12_out, DS_7, DS_7);
  nand nand_13 (nand_13_out, nand_1_out, nand_2_out);
  nand nand_14 (nand_14_out, nand_3_out, nand_4_out);
  nand nand_15 (nand_15_out, nand_5_out, nand_6_out);
  nand nand_16 (nand_16_out, nand_7_out, nand_8_out);
  nand nand_17 (nand_17_out, nand_9_out, nand_10_out);
  nand nand_18 (nand_18_out, nand_11_out, nand_12_out);
  nand nand_19 (nand_19_out, nand_13_out, nand_13_out);
  nand nand_20 (nand_20_out, DS_2, DS_2);
  nand nand_21 (nand_21_out, nand_14_out, nand_14_out);
  nand nand_22 (nand_22_out, DS_5, DS_5);
  nand nand_23 (nand_23_out, nand_15_out, nand_15_out);
  nand nand_24 (nand_24_out, DS_8, DS_8);
  nand nand_25 (nand_25_out, DS_9, DS_9);
  nand nand_26 (nand_26_out, nand_16_out, nand_16_out);
  nand nand_27 (nand_27_out, DS_2, DS_2);
  nand nand_28 (nand_28_out, nand_17_out, nand_17_out);
  nand nand_29 (nand_29_out, DS_5, DS_5);
  nand nand_30 (nand_30_out, nand_18_out, nand_18_out);
  nand nand_31 (nand_31_out, DS_8, DS_8);
  nand nand_32 (nand_32_out, DS_9, DS_9);
  nand nand_33 (nand_33_out, nand_19_out, nand_20_out);
  nand nand_34 (nand_34_out, nand_21_out, nand_22_out);
  nand nand_35 (nand_35_out, nand_23_out, nand_24_out);
  nand nand_36 (nand_36_out, nand_25_out, B_1);
  nand nand_37 (nand_37_out, nand_26_out, nand_27_out);
  nand nand_38 (nand_38_out, nand_28_out, nand_29_out);
  nand nand_39 (nand_39_out, nand_30_out, nand_31_out);
  nand nand_40 (nand_40_out, nand_32_out, B_0);
  nand nand_41 (nand_41_out, nand_33_out, nand_33_out);
  nand nand_42 (nand_42_out, nand_34_out, nand_34_out);
  nand nand_43 (nand_43_out, nand_35_out, nand_35_out);
  nand nand_44 (nand_44_out, nand_36_out, nand_36_out);
  nand nand_45 (nand_45_out, nand_37_out, nand_37_out);
  nand nand_46 (nand_46_out, nand_38_out, nand_38_out);
  nand nand_47 (nand_47_out, nand_39_out, nand_39_out);
  nand nand_48 (nand_48_out, nand_40_out, nand_40_out);
  nand nand_49 (nand_49_out, nand_41_out, nand_42_out);
  nand nand_50 (nand_50_out, nand_43_out, nand_44_out);
  nand nand_51 (nand_51_out, nand_45_out, nand_46_out);
  nand nand_52 (nand_52_out, nand_47_out, nand_48_out);
  nand nand_53 (nand_53_out, nand_49_out, nand_49_out);
  nand nand_54 (nand_54_out, nand_50_out, nand_50_out);
  nand nand_55 (nand_55_out, nand_51_out, nand_51_out);
  nand nand_56 (nand_56_out, nand_52_out, nand_52_out);
  nand nand_57 (nand_57_out, nand_53_out, nand_54_out);
  nand nand_58 (nand_58_out, nand_55_out, nand_56_out);
  nand nand_59 (O_1, nand_57_out, nand_57_out);
  nand nand_60 (O_0, nand_58_out, nand_58_out);
endmodule

module memory_time (
  input  [29:0] I_0,
  input  clock_in,
  input  reset,
  input  [3:0] load,
  output carry,
  output [29:0] O_0
);

  wire and_1_out, clock_1_out, comparator_1_eq, comparator_2_eq, comparator_3_eq, comparator_4_eq,
       multiplexer_1_out, or_1_out;
  wire [5:0] binary_to_time_converter_1_output_bus_1, binary_to_time_converter_2_output_bus_1,
       binary_to_time_converter_3_output_bus_1, counter_1_q, counter_2_q, counter_3_q;

  Comparator #(.width(4)) comparator_1 (.a(load), .b(4'b0011), .eq(comparator_1_eq));  // open: gt, lt
  Comparator #(.width(4)) comparator_2 (.a(load), .b(4'b0111), .eq(comparator_2_eq));  // open: gt, lt
  binary_to_time_converter binary_to_time_converter_1 (
    .Input_bus_1(I_0[29:25]), .Input_bus_2(I_0[24:20]), .Output_bus_1(binary_to_time_converter_1_output_bus_1));
  binary_to_time_converter binary_to_time_converter_2 (
    .Input_bus_1(I_0[19:15]), .Input_bus_2(I_0[14:10]), .Output_bus_1(binary_to_time_converter_2_output_bus_1));
  binary_to_time_converter binary_to_time_converter_3 (
    .Input_bus_1(I_0[9:5]), .Input_bus_2(I_0[4:0]), .Output_bus_1(binary_to_time_converter_3_output_bus_1));
  Clock #(.highDuration(40), .lowDuration(40)) clock_1 (.out(clock_1_out));
  or or_1 (or_1_out, comparator_1_eq, comparator_2_eq);
  Multiplexer #(.enable("false")) multiplexer_1 (
    .in0(clock_in), .in1(clock_1_out), .out(multiplexer_1_out), .sel(or_1_out));
  Counter #(.width(6), .max('h17)) counter_1 (
    .clr(reset), .load(or_1_out), .up(1'b1), .count(and_1_out), .clk(multiplexer_1_out),
    .D(binary_to_time_converter_1_output_bus_1), .Q(counter_1_q));  // open: carry
  Counter #(.width(6), .max('h3b)) counter_2 (
    .clr(reset), .load(or_1_out), .up(1'b1), .count(comparator_3_eq), .clk(multiplexer_1_out),
    .D(binary_to_time_converter_2_output_bus_1), .Q(counter_2_q));  // open: carry
  Counter #(.width(6), .max('h3b)) counter_3 (
    .clr(reset), .load(or_1_out), .up(1'b1), .count(1'b1), .clk(multiplexer_1_out),
    .D(binary_to_time_converter_3_output_bus_1), .Q(counter_3_q));  // open: carry
  Comparator #(.width(6)) comparator_3 (.a(6'b111011), .b(counter_3_q), .eq(comparator_3_eq));  // open: gt, lt
  and and_1 (and_1_out, comparator_4_eq, comparator_3_eq);
  Comparator #(.width(6)) comparator_4 (.a(6'b111011), .b(counter_2_q), .eq(comparator_4_eq));  // open: gt, lt
  Comparator #(.width(6)) comparator_5 (.a(6'b010111), .b(counter_1_q), .eq(carry));  // open: gt, lt
  time_to_binary_converter time_to_binary_converter_1 (.t_in(counter_1_q), .O_1(O_0[29:25]), .O_0(O_0[24:20]));
  time_to_binary_converter time_to_binary_converter_2 (.t_in(counter_2_q), .O_1(O_0[19:15]), .O_0(O_0[14:10]));
  time_to_binary_converter time_to_binary_converter_3 (.t_in(counter_3_q), .O_1(O_0[9:5]), .O_0(O_0[4:0]));
endmodule

module inc_6bits (
  input  I_5,
  input  I_4,
  input  I_3,
  input  I_2,
  input  I_1,
  input  I_0,
  input  c_in,
  output c_out,
  output O_5,
  output O_4,
  output O_3,
  output O_2,
  output O_1,
  output O_0
);

  wire half_adder_2_ci, half_adder_3_ci, half_adder_4_ci, half_adder_5_ci, half_adder_6_ci;

  half_adder half_adder_1 (.ai(I_5), .bi(half_adder_2_ci), .si(O_5), .ci(c_out));
  half_adder half_adder_2 (.ai(I_4), .bi(half_adder_3_ci), .si(O_4), .ci(half_adder_2_ci));
  half_adder half_adder_3 (.ai(I_3), .bi(half_adder_4_ci), .si(O_3), .ci(half_adder_3_ci));
  half_adder half_adder_4 (.ai(I_2), .bi(half_adder_5_ci), .si(O_2), .ci(half_adder_4_ci));
  half_adder half_adder_5 (.ai(I_1), .bi(half_adder_6_ci), .si(O_1), .ci(half_adder_5_ci));
  half_adder half_adder_6 (.ai(I_0), .bi(c_in), .si(O_0), .ci(half_adder_6_ci));
endmodule

module half_adder (
  input  ai,
  input  bi,
  output si,
  output ci
);

  xor xor_1 (si, ai, bi);
  and and_1 (ci, ai, bi);
endmodule

module full_adder (
  input  ai,
  input  bi,
  input  ciminus1,
  output si,
  output ci
);

  wire and_4_out, nand_1_out, nand_2_out, nand_3_out, xor_1_out;

  xor xor_1 (xor_1_out, ai, bi);
  // AND_Gate and_1 has open pins: in0=ai, in1=bi, out=open
  nand nand_1 (nand_1_out, ai, bi);
  nand nand_2 (nand_2_out, ai, ciminus1);
  // AND_Gate and_2 has open pins: in0=ai, in1=ciminus1, out=open
  // AND_Gate and_3 has open pins: in0=bi, in1=ciminus1, out=open
  nand nand_3 (nand_3_out, bi, ciminus1);
  xor xor_2 (si, xor_1_out, ciminus1);
  and and_4 (and_4_out, nand_1_out, nand_2_out);
  nand nand_4 (ci, and_4_out, nand_3_out);
endmodule

module set_time_setter (
  input  [29:0] I_0,
  input  [11:0] input_bus,
  input  mode_on,
  input  R,
  output [29:0] O_0
);

  wire not_1_out;

  not not_1 (not_1_out, mode_on);
  set_time_to_23 set_time_to_23_1 (
    .R(R), .B_1(input_bus[11]), .B_0(input_bus[10]), .load(not_1_out), .set_on(input_bus[4]),
    .I_1(I_0[29:25]), .I_0(I_0[24:20]), .O_1(O_0[29:25]), .O_0(O_0[24:20]));
  set_time_to_5 set_time_to_5_1 (
    .R(R), .B_1(input_bus[11]), .B_0(input_bus[10]), .load(not_1_out), .set_on(input_bus[3]),
    .I_0(I_0[19:15]), .O_0(O_0[19:15]));
  set_time_to_9 set_time_to_9_1 (
    .R(R), .B_1(input_bus[11]), .B_0(input_bus[10]), .load(not_1_out), .set_on(input_bus[2]),
    .I_0(I_0[14:10]), .O_0(O_0[14:10]));
  set_time_to_5 set_time_to_5_2 (
    .R(R), .B_1(input_bus[11]), .B_0(input_bus[10]), .load(not_1_out), .set_on(input_bus[1]), .I_0(I_0[9:5]),
    .O_0(O_0[9:5]));
  set_time_to_9 set_time_to_9_2 (
    .R(R), .B_1(input_bus[11]), .B_0(input_bus[10]), .load(not_1_out), .set_on(input_bus[0]), .I_0(I_0[4:0]),
    .O_0(O_0[4:0]));
endmodule

module set_time_to_9 (
  input  R,
  input  B_1,
  input  B_0,
  input  load,
  input  set_on,
  input  [4:0] I_0,
  output [4:0] O_0
);

  wire and_1_out, clock_1_out, or_1_out;

  Clock clock_1 (.out(clock_1_out));
  or or_1 (or_1_out, B_1, B_0);
  and and_1 (and_1_out, or_1_out, set_on);
  Counter #(.width(5), .max('h9)) counter_1 (
    .clr(R), .load(load), .up(B_0), .count(and_1_out), .clk(clock_1_out), .D(I_0), .Q(O_0));  // open: carry
endmodule

module set_time_to_5 (
  input  R,
  input  B_1,
  input  B_0,
  input  load,
  input  set_on,
  input  [4:0] I_0,
  output [4:0] O_0
);

  wire and_1_out, C_out, or_1_out;

  Clock C (.out(C_out));
  or or_1 (or_1_out, B_1, B_0);
  and and_1 (and_1_out, or_1_out, set_on);
  Counter #(.width(5), .max('h5)) counter_1 (
    .clr(R), .load(load), .up(B_0), .count(and_1_out), .clk(C_out), .D(I_0), .Q(O_0));  // open: carry
endmodule

module set_time_to_23 (
  input  R,
  input  B_1,
  input  B_0,
  input  load,
  input  set_on,
  input  [4:0] I_1,
  input  [4:0] I_0,
  output [4:0] O_1,
  output [4:0] O_0
);

  wire and_1_out, and_2_out, and_3_out, and_4_out, and_5_out, and_6_out, C_out, comparator_1_eq,
       comparator_2_eq, counter_1_carry, counter_2_carry, or_1_out, or_2_out, or_3_out, or_4_out;
  wire [4:0] multiplexer_1_out, multiplexer_2_out;

  Clock C (.out(C_out));
  or or_1 (or_1_out, B_1, B_0);
  and and_1 (and_1_out, or_1_out, set_on);
  or or_2 (or_2_out, and_2_out, and_5_out, and_3_out);
  and and_2 (and_2_out, and_1_out, counter_2_carry);
  or or_3 (or_3_out, and_3_out, and_5_out);
  or or_4 (or_4_out, or_3_out, load);
  Multiplexer #(.width(5), .enable("false")) multiplexer_1 (
    .in0(I_0), .in1(multiplexer_2_out), .out(multiplexer_1_out), .sel(or_3_out));
  Multiplexer #(.width(5), .enable("false")) multiplexer_2 (
    .in0({5{1'b0}}), .in1(5'b00011), .out(multiplexer_2_out), .sel(and_5_out));
  Counter #(.width(5), .max('h2)) counter_1 (
    .clr(R), .load(load), .up(B_0), .count(or_2_out), .clk(C_out), .D(I_1), .carry(counter_1_carry), .Q(O_1));
  and and_3 (and_3_out, counter_1_carry, and_4_out);
  and and_4 (and_4_out, comparator_2_eq, ~B_1, B_0, set_on);  // AND_Gate
  and and_5 (and_5_out, counter_1_carry, and_6_out);
  and and_6 (and_6_out, ~B_0, B_1, comparator_1_eq, set_on);  // AND_Gate
  Counter #(.width(5), .max('h9)) counter_2 (
    .clr(R), .load(or_4_out), .up(B_0), .count(and_1_out), .clk(C_out), .D(multiplexer_1_out),
    .carry(counter_2_carry), .Q(O_0));
  Comparator #(.width(5)) comparator_1 (.a({5{1'b0}}), .b(O_0), .eq(comparator_1_eq));  // open: gt, lt
  Comparator #(.width(5)) comparator_2 (.a(5'b00011), .b(O_0), .eq(comparator_2_eq));  // open: gt, lt
endmodule

module time_to_binary_converter (
  input  [5:0] t_in,
  output [4:0] O_1,
  output [4:0] O_0
);

  wire nand_1_out, nand_2_out, nand_3_out, nand_4_out, nand_5_out, nand_6_out, nand_7_out, nand_8_out,
       nand_9_out, nand_10_out, nand_11_out, nand_12_out, nand_13_out, nand_14_out, nand_15_out, nand_16_out,
       nand_17_out, nand_18_out, nand_19_out, nand_20_out, nand_21_out, nand_22_out, nand_23_out,
       nand_24_out, nand_25_out, nand_26_out, nand_27_out, nand_28_out, nand_29_out, nand_30_out,
       nand_31_out, nand_32_out, nand_33_out, nand_34_out, nand_35_out, nand_36_out, nand_37_out,
       nand_38_out, nand_39_out, nand_40_out, nand_41_out, nand_42_out, nand_43_out, nand_44_out,
       nand_45_out, nand_46_out, nand_47_out, nand_48_out, nand_49_out, nand_50_out, nand_51_out,
       nand_52_out, nand_53_out, nand_54_out, nand_56_out, nand_57_out, nand_58_out, nand_59_out,
       nand_60_out, nand_61_out, nand_62_out, nand_63_out, nand_64_out, nand_65_out, nand_66_out,
       nand_67_out, nand_68_out, nand_69_out, nand_70_out, nand_71_out, nand_72_out, nand_73_out,
       nand_74_out, nand_75_out, nand_76_out, nand_77_out, nand_78_out, nand_79_out, nand_80_out,
       nand_81_out, nand_82_out, nand_83_out, nand_84_out, nand_85_out, nand_86_out, nand_87_out,
       nand_88_out, nand_89_out, nand_90_out, nand_91_out, nand_92_out, nand_93_out, nand_94_out,
       nand_95_out, nand_96_out, nand_97_out, nand_98_out, nand_99_out, nand_100_out, nand_101_out,
       nand_102_out, nand_103_out, nand_104_out, nand_105_out, nand_106_out, nand_107_out, nand_108_out,
       nand_109_out, nand_110_out, nand_111_out, nand_112_out, nand_113_out, nand_114_out, nand_115_out,
       nand_116_out, nand_117_out, nand_118_out, nand_119_out, nand_120_out, nand_121_out, nand_122_out,
       nand_123_out, nand_124_out, nand_125_out, nand_126_out, nand_127_out, nand_128_out, nand_129_out,
       nand_130_out, nand_131_out, nand_132_out, nand_133_out, nand_134_out, nand_135_out, nand_136_out,
       nand_137_out, nand_138_out, nand_139_out, nand_140_out, nand_141_out, nand_142_out, nand_143_out,
       nand_144_out, nand_145_out, nand_146_out, nand_147_out, nand_148_out, nand_149_out, nand_150_out,
       nand_151_out, nand_152_out, nand_153_out, nand_154_out, nand_155_out, nand_156_out, nand_157_out,
       nand_158_out, nand_159_out, nand_160_out, nand_161_out, nand_162_out, nand_163_out, nand_164_out,
       nand_165_out, nand_166_out, nand_167_out, nand_168_out, nand_169_out, nand_170_out, nand_171_out,
       nand_172_out, nand_173_out, nand_174_out, nand_175_out, nand_176_out, nand_177_out, nand_178_out,
       nand_179_out, nand_180_out, nand_181_out, nand_182_out, nand_183_out, nand_184_out, nand_185_out,
       nand_186_out, nand_187_out, nand_188_out, nand_189_out, nand_190_out, nand_191_out, nand_192_out,
       nand_193_out, nand_194_out, nand_195_out, nand_196_out, nand_197_out, nand_198_out, nand_199_out,
       nand_200_out, nand_201_out, nand_202_out, nand_203_out, nand_204_out, nand_205_out, nand_206_out,
       nand_207_out, nand_208_out, nand_209_out, nand_210_out, nand_211_out, nand_212_out, nand_213_out,
       nand_214_out, nand_215_out, nand_216_out, nand_217_out, nand_218_out, nand_219_out, nand_220_out,
       nand_221_out, nand_222_out, nand_223_out, nand_224_out, nand_225_out, nand_226_out, nand_227_out,
       nand_228_out, nand_229_out, nand_230_out, nand_231_out, nand_232_out, nand_233_out, nand_234_out,
       nand_235_out, nand_236_out, nand_237_out, nand_238_out, nand_239_out, nand_240_out, nand_241_out,
       nand_242_out, nand_243_out, nand_244_out, nand_245_out, nand_246_out, nand_247_out, nand_248_out,
       nand_249_out, nand_250_out, nand_251_out, nand_252_out, nand_253_out, nand_254_out, nand_255_out,
       nand_256_out, nand_257_out, nand_258_out, nand_259_out, nand_260_out, nand_261_out, nand_262_out,
       nand_263_out, nand_264_out, nand_265_out, nand_266_out, nand_267_out, nand_268_out, nand_269_out,
       nand_270_out, nand_271_out, nand_272_out, nand_273_out, nand_274_out, nand_275_out, nand_276_out,
       nand_277_out, nand_278_out, nand_279_out, nand_280_out, nand_281_out, nand_282_out, nand_283_out,
       nand_284_out, nand_285_out, nand_286_out, nand_287_out, nand_288_out, nand_290_out, nand_291_out,
       nand_292_out, nand_293_out, nand_294_out, nand_295_out, nand_296_out, nand_297_out, nand_298_out,
       nand_299_out, nand_300_out, nand_301_out, nand_302_out, nand_303_out, nand_304_out, nand_305_out,
       nand_306_out, nand_307_out, nand_308_out, nand_309_out, nand_310_out, nand_311_out, nand_313_out,
       nand_314_out, nand_315_out, nand_316_out, nand_317_out, nand_318_out;

  nand nand_1 (nand_1_out, t_in[5], t_in[5]);
  nand nand_2 (nand_2_out, t_in[4], t_in[4]);
  nand nand_3 (nand_3_out, t_in[5], t_in[5]);
  nand nand_4 (nand_4_out, t_in[4], t_in[4]);
  nand nand_5 (nand_5_out, t_in[4], t_in[4]);
  nand nand_6 (nand_6_out, t_in[5], t_in[5]);
  nand nand_7 (nand_7_out, t_in[4], t_in[4]);
  nand nand_8 (nand_8_out, t_in[3], t_in[3]);
  nand nand_9 (nand_9_out, t_in[5], t_in[5]);
  nand nand_10 (nand_10_out, t_in[3], t_in[3]);
  nand nand_11 (nand_11_out, t_in[5], t_in[5]);
  nand nand_12 (nand_12_out, t_in[4], t_in[4]);
  nand nand_13 (nand_13_out, t_in[5], t_in[5]);
  nand nand_14 (nand_14_out, t_in[5], t_in[5]);
  nand nand_15 (nand_15_out, t_in[4], t_in[4]);
  nand nand_16 (nand_16_out, t_in[3], t_in[3]);
  nand nand_17 (nand_17_out, t_in[1], t_in[1]);
  nand nand_18 (nand_18_out, t_in[3], t_in[3]);
  nand nand_19 (nand_19_out, t_in[1], t_in[1]);
  nand nand_20 (nand_20_out, t_in[5], t_in[3]);
  nand nand_21 (nand_21_out, t_in[5], t_in[4]);
  nand nand_22 (nand_22_out, t_in[5], t_in[5]);
  nand nand_23 (nand_23_out, t_in[5], t_in[5]);
  nand nand_24 (nand_24_out, t_in[4], t_in[4]);
  nand nand_25 (nand_25_out, t_in[5], t_in[5]);
  nand nand_26 (nand_26_out, t_in[4], t_in[4]);
  nand nand_27 (nand_27_out, t_in[5], t_in[5]);
  nand nand_28 (nand_28_out, t_in[4], t_in[4]);
  nand nand_29 (nand_29_out, t_in[5], t_in[5]);
  nand nand_30 (nand_30_out, t_in[5], t_in[5]);
  nand nand_31 (nand_31_out, t_in[3], t_in[3]);
  nand nand_32 (nand_32_out, t_in[2], t_in[2]);
  nand nand_33 (nand_33_out, t_in[4], t_in[4]);
  nand nand_34 (nand_34_out, t_in[3], t_in[3]);
  nand nand_35 (nand_35_out, t_in[3], t_in[3]);
  nand nand_36 (nand_36_out, t_in[2], t_in[2]);
  nand nand_37 (nand_37_out, nand_1_out, nand_2_out);
  nand nand_38 (nand_38_out, nand_3_out, t_in[4]);
  nand nand_39 (nand_39_out, t_in[5], nand_4_out);
  nand nand_40 (nand_40_out, t_in[5], t_in[4]);
  nand nand_41 (nand_41_out, t_in[5], nand_5_out);
  nand nand_42 (nand_42_out, t_in[5], t_in[4]);
  nand nand_43 (nand_43_out, nand_6_out, nand_7_out);
  nand nand_44 (nand_44_out, nand_8_out, t_in[1]);
  nand nand_45 (nand_45_out, nand_9_out, nand_10_out);
  nand nand_46 (nand_46_out, t_in[2], t_in[1]);
  nand nand_47 (nand_47_out, nand_11_out, nand_12_out);
  nand nand_48 (nand_48_out, nand_13_out, t_in[4]);
  nand nand_49 (nand_49_out, nand_14_out, t_in[4]);
  nand nand_50 (nand_50_out, t_in[5], nand_15_out);
  nand nand_51 (nand_51_out, nand_16_out, nand_17_out);
  nand nand_52 (nand_52_out, t_in[5], nand_18_out);
  nand nand_53 (nand_53_out, t_in[2], nand_19_out);
  nand nand_54 (nand_54_out, t_in[5], t_in[4]);
  nand nand_55 (O_1[2], nand_20_out, nand_21_out);
  nand nand_56 (nand_56_out, nand_22_out, t_in[4]);
  nand nand_57 (nand_57_out, nand_23_out, t_in[4]);
  nand nand_58 (nand_58_out, t_in[4], t_in[3]);
  nand nand_59 (nand_59_out, t_in[5], nand_24_out);
  nand nand_60 (nand_60_out, nand_25_out, nand_26_out);
  nand nand_61 (nand_61_out, t_in[3], t_in[1]);
  nand nand_62 (nand_62_out, nand_27_out, nand_28_out);
  nand nand_63 (nand_63_out, t_in[3], t_in[2]);
  nand nand_64 (nand_64_out, nand_29_out, t_in[3]);
  nand nand_65 (nand_65_out, t_in[2], t_in[1]);
  nand nand_66 (nand_66_out, nand_30_out, t_in[4]);
  nand nand_67 (nand_67_out, nand_31_out, nand_32_out);
  nand nand_68 (nand_68_out, t_in[5], nand_33_out);
  nand nand_69 (nand_69_out, t_in[5], nand_34_out);
  nand nand_70 (nand_70_out, t_in[5], nand_35_out);
  nand nand_71 (nand_71_out, t_in[5], t_in[4]);
  nand nand_72 (nand_72_out, t_in[3], nand_36_out);
  nand nand_73 (nand_73_out, nand_37_out, nand_37_out);
  nand nand_74 (nand_74_out, t_in[2], t_in[2]);
  nand nand_75 (nand_75_out, t_in[1], t_in[1]);
  nand nand_76 (nand_76_out, nand_38_out, nand_38_out);
  nand nand_77 (nand_77_out, t_in[3], t_in[3]);
  nand nand_78 (nand_78_out, t_in[2], t_in[2]);
  nand nand_79 (nand_79_out, t_in[5], t_in[5]);
  nand nand_80 (nand_80_out, nand_39_out, nand_39_out);
  nand nand_81 (nand_81_out, t_in[3], t_in[3]);
  nand nand_82 (nand_82_out, nand_40_out, nand_40_out);
  nand nand_83 (nand_83_out, t_in[3], t_in[3]);
  nand nand_84 (nand_84_out, t_in[2], t_in[2]);
  nand nand_85 (nand_85_out, t_in[1], t_in[1]);
  nand nand_86 (nand_86_out, t_in[4], t_in[4]);
  nand nand_87 (nand_87_out, t_in[3], t_in[3]);
  nand nand_88 (nand_88_out, t_in[1], t_in[1]);
  nand nand_89 (nand_89_out, t_in[5], t_in[5]);
  nand nand_90 (nand_90_out, t_in[4], t_in[4]);
  nand nand_91 (nand_91_out, t_in[5], t_in[5]);
  nand nand_92 (nand_92_out, t_in[2], t_in[2]);
  nand nand_93 (nand_93_out, t_in[1], t_in[1]);
  nand nand_94 (nand_94_out, t_in[5], t_in[5]);
  nand nand_95 (nand_95_out, t_in[2], t_in[2]);
  nand nand_96 (nand_96_out, t_in[2], t_in[2]);
  nand nand_97 (nand_97_out, t_in[1], t_in[1]);
  nand nand_98 (nand_98_out, nand_41_out, nand_41_out);
  nand nand_99 (nand_99_out, t_in[3], t_in[3]);
  nand nand_100 (nand_100_out, t_in[2], t_in[2]);
  nand nand_101 (nand_101_out, t_in[4], t_in[4]);
  nand nand_102 (nand_102_out, nand_42_out, nand_42_out);
  nand nand_103 (nand_103_out, t_in[3], t_in[3]);
  nand nand_104 (nand_104_out, nand_43_out, nand_43_out);
  nand nand_105 (nand_105_out, nand_44_out, nand_44_out);
  nand nand_106 (nand_106_out, nand_45_out, nand_45_out);
  nand nand_107 (nand_107_out, nand_46_out, nand_46_out);
  nand nand_108 (nand_108_out, nand_47_out, nand_47_out);
  nand nand_109 (nand_109_out, t_in[1], t_in[1]);
  nand nand_110 (nand_110_out, nand_48_out, nand_48_out);
  nand nand_111 (nand_111_out, t_in[3], t_in[3]);
  nand nand_112 (nand_112_out, t_in[2], t_in[2]);
  nand nand_113 (nand_113_out, t_in[1], t_in[1]);
  nand nand_114 (nand_114_out, nand_49_out, nand_49_out);
  nand nand_115 (nand_115_out, t_in[2], t_in[2]);
  nand nand_116 (nand_116_out, nand_50_out, nand_50_out);
  nand nand_117 (nand_117_out, nand_51_out, nand_51_out);
  nand nand_118 (nand_118_out, nand_52_out, nand_52_out);
  nand nand_119 (nand_119_out, nand_53_out, nand_53_out);
  nand nand_120 (nand_120_out, t_in[4], t_in[4]);
  nand nand_121 (nand_121_out, nand_54_out, nand_54_out);
  nand nand_122 (nand_122_out, t_in[2], t_in[2]);
  nand nand_123 (nand_123_out, t_in[1], t_in[1]);
  nand nand_124 (nand_124_out, nand_56_out, nand_56_out);
  nand nand_125 (nand_125_out, nand_57_out, nand_57_out);
  nand nand_126 (nand_126_out, nand_58_out, nand_58_out);
  nand nand_127 (nand_127_out, nand_59_out, nand_59_out);
  nand nand_128 (nand_128_out, t_in[3], t_in[3]);
  nand nand_129 (nand_129_out, nand_60_out, nand_60_out);
  nand nand_130 (nand_130_out, nand_61_out, nand_61_out);
  nand nand_131 (nand_131_out, nand_62_out, nand_62_out);
  nand nand_132 (nand_132_out, nand_63_out, nand_63_out);
  nand nand_133 (nand_133_out, nand_64_out, nand_64_out);
  nand nand_134 (nand_134_out, nand_65_out, nand_65_out);
  nand nand_135 (nand_135_out, nand_66_out, nand_66_out);
  nand nand_136 (nand_136_out, nand_67_out, nand_67_out);
  nand nand_137 (nand_137_out, nand_68_out, nand_68_out);
  nand nand_138 (nand_138_out, t_in[3], t_in[3]);
  nand nand_139 (nand_139_out, nand_69_out, nand_69_out);
  nand nand_140 (nand_140_out, nand_70_out, nand_70_out);
  nand nand_141 (nand_141_out, nand_71_out, nand_71_out);
  nand nand_142 (nand_142_out, nand_72_out, nand_72_out);
  nand nand_143 (nand_143_out, nand_73_out, t_in[3]);
  nand nand_144 (nand_144_out, nand_74_out, nand_75_out);
  nand nand_145 (nand_145_out, nand_76_out, nand_77_out);
  nand nand_146 (nand_146_out, nand_78_out, t_in[1]);
  nand nand_147 (nand_147_out, nand_79_out, t_in[4]);
  nand nand_148 (nand_148_out, nand_80_out, nand_81_out);
  nand nand_149 (nand_149_out, t_in[2], t_in[1]);
  nand nand_150 (nand_150_out, nand_82_out, nand_83_out);
  nand nand_151 (nand_151_out, nand_84_out, nand_85_out);
  nand nand_152 (nand_152_out, t_in[5], t_in[4]);
  nand nand_153 (nand_153_out, nand_86_out, nand_87_out);
  nand nand_154 (nand_154_out, t_in[2], nand_88_out);
  nand nand_155 (nand_155_out, nand_89_out, nand_90_out);
  nand nand_156 (nand_156_out, t_in[2], t_in[1]);
  nand nand_157 (nand_157_out, nand_91_out, t_in[4]);
  nand nand_158 (nand_158_out, nand_92_out, nand_93_out);
  nand nand_159 (nand_159_out, nand_94_out, t_in[4]);
  nand nand_160 (nand_160_out, t_in[3], nand_95_out);
  nand nand_161 (nand_161_out, t_in[4], t_in[3]);
  nand nand_162 (nand_162_out, nand_96_out, nand_97_out);
  nand nand_163 (nand_163_out, nand_98_out, nand_99_out);
  nand nand_164 (nand_164_out, nand_100_out, t_in[1]);
  nand nand_165 (nand_165_out, t_in[5], nand_101_out);
  nand nand_166 (nand_166_out, t_in[3], t_in[2]);
  nand nand_167 (nand_167_out, nand_102_out, nand_103_out);
  nand nand_168 (nand_168_out, t_in[2], t_in[1]);
  nand nand_169 (nand_169_out, nand_104_out, nand_105_out);
  nand nand_170 (nand_170_out, nand_106_out, nand_107_out);
  nand nand_171 (nand_171_out, nand_108_out, t_in[3]);
  nand nand_172 (nand_172_out, t_in[2], nand_109_out);
  nand nand_173 (nand_173_out, nand_110_out, nand_111_out);
  nand nand_174 (nand_174_out, nand_112_out, nand_113_out);
  nand nand_175 (nand_175_out, nand_114_out, t_in[3]);
  nand nand_176 (nand_176_out, nand_115_out, t_in[1]);
  nand nand_177 (nand_177_out, nand_116_out, nand_117_out);
  nand nand_178 (nand_178_out, nand_118_out, nand_119_out);
  nand nand_179 (nand_179_out, t_in[5], nand_120_out);
  nand nand_180 (nand_180_out, t_in[3], t_in[1]);
  nand nand_181 (nand_181_out, t_in[5], t_in[3]);
  nand nand_182 (nand_182_out, t_in[2], t_in[1]);
  nand nand_183 (nand_183_out, nand_121_out, t_in[3]);
  nand nand_184 (nand_184_out, nand_122_out, nand_123_out);
  nand nand_185 (nand_185_out, nand_124_out, t_in[2]);
  nand nand_186 (nand_186_out, nand_125_out, t_in[3]);
  nand nand_187 (nand_187_out, nand_126_out, t_in[2]);
  nand nand_188 (nand_188_out, nand_127_out, nand_128_out);
  nand nand_189 (nand_189_out, nand_129_out, nand_130_out);
  nand nand_190 (nand_190_out, nand_131_out, nand_132_out);
  nand nand_191 (nand_191_out, nand_133_out, nand_134_out);
  nand nand_192 (nand_192_out, nand_135_out, nand_136_out);
  nand nand_193 (nand_193_out, nand_137_out, nand_138_out);
  nand nand_194 (nand_194_out, nand_139_out, t_in[1]);
  nand nand_195 (nand_195_out, nand_140_out, t_in[2]);
  nand nand_196 (nand_196_out, nand_141_out, nand_142_out);
  nand nand_197 (nand_197_out, nand_143_out, nand_143_out);
  nand nand_198 (nand_198_out, nand_144_out, nand_144_out);
  nand nand_199 (nand_199_out, nand_145_out, nand_145_out);
  nand nand_200 (nand_200_out, nand_146_out, nand_146_out);
  nand nand_201 (nand_201_out, nand_147_out, nand_147_out);
  nand nand_202 (nand_202_out, t_in[1], t_in[1]);
  nand nand_203 (nand_203_out, nand_148_out, nand_148_out);
  nand nand_204 (nand_204_out, nand_149_out, nand_149_out);
  nand nand_205 (nand_205_out, nand_150_out, nand_150_out);
  nand nand_206 (nand_206_out, nand_151_out, nand_151_out);
  nand nand_207 (nand_207_out, nand_152_out, nand_152_out);
  nand nand_208 (nand_208_out, t_in[2], t_in[2]);
  nand nand_209 (nand_209_out, nand_153_out, nand_153_out);
  nand nand_210 (nand_210_out, nand_154_out, nand_154_out);
  nand nand_211 (nand_211_out, nand_155_out, nand_155_out);
  nand nand_212 (nand_212_out, nand_156_out, nand_156_out);
  nand nand_213 (nand_213_out, nand_157_out, nand_157_out);
  nand nand_214 (nand_214_out, nand_158_out, nand_158_out);
  nand nand_215 (nand_215_out, nand_159_out, nand_159_out);
  nand nand_216 (nand_216_out, nand_160_out, nand_160_out);
  nand nand_217 (nand_217_out, nand_161_out, nand_161_out);
  nand nand_218 (nand_218_out, nand_162_out, nand_162_out);
  nand nand_219 (nand_219_out, nand_163_out, nand_163_out);
  nand nand_220 (nand_220_out, nand_164_out, nand_164_out);
  nand nand_221 (nand_221_out, nand_165_out, nand_165_out);
  nand nand_222 (nand_222_out, nand_166_out, nand_166_out);
  nand nand_223 (nand_223_out, nand_167_out, nand_167_out);
  nand nand_224 (nand_224_out, nand_168_out, nand_168_out);
  nand nand_225 (nand_225_out, nand_169_out, nand_170_out);
  nand nand_226 (nand_226_out, nand_171_out, nand_171_out);
  nand nand_227 (nand_227_out, nand_172_out, nand_172_out);
  nand nand_228 (nand_228_out, nand_173_out, nand_173_out);
  nand nand_229 (nand_229_out, nand_174_out, nand_174_out);
  nand nand_230 (nand_230_out, nand_175_out, nand_175_out);
  nand nand_231 (nand_231_out, nand_176_out, nand_176_out);
  nand nand_232 (nand_232_out, nand_177_out, nand_178_out);
  nand nand_233 (nand_233_out, nand_179_out, nand_179_out);
  nand nand_234 (nand_234_out, nand_180_out, nand_180_out);
  nand nand_235 (nand_235_out, nand_181_out, nand_181_out);
  nand nand_236 (nand_236_out, nand_182_out, nand_182_out);
  nand nand_237 (nand_237_out, nand_183_out, nand_183_out);
  nand nand_238 (nand_238_out, nand_184_out, nand_184_out);
  nand nand_239 (nand_239_out, nand_185_out, nand_186_out);
  nand nand_240 (nand_240_out, nand_187_out, nand_188_out);
  nand nand_241 (nand_241_out, nand_189_out, nand_190_out);
  nand nand_242 (nand_242_out, nand_191_out, nand_192_out);
  nand nand_243 (nand_243_out, nand_193_out, nand_194_out);
  nand nand_244 (nand_244_out, nand_195_out, nand_196_out);
  nand nand_245 (nand_245_out, nand_197_out, nand_198_out);
  nand nand_246 (nand_246_out, nand_199_out, nand_200_out);
  nand nand_247 (nand_247_out, nand_201_out, t_in[3]);
  nand nand_248 (nand_248_out, t_in[2], nand_202_out);
  nand nand_249 (nand_249_out, nand_203_out, nand_204_out);
  nand nand_250 (nand_250_out, nand_205_out, nand_206_out);
  nand nand_251 (nand_251_out, nand_207_out, t_in[3]);
  nand nand_252 (nand_252_out, nand_208_out, t_in[1]);
  nand nand_253 (nand_253_out, nand_209_out, nand_210_out);
  nand nand_254 (nand_254_out, nand_211_out, nand_212_out);
  nand nand_255 (nand_255_out, nand_213_out, nand_214_out);
  nand nand_256 (nand_256_out, nand_215_out, nand_216_out);
  nand nand_257 (nand_257_out, nand_217_out, nand_218_out);
  nand nand_258 (nand_258_out, nand_219_out, nand_220_out);
  nand nand_259 (nand_259_out, nand_221_out, nand_222_out);
  nand nand_260 (nand_260_out, nand_223_out, nand_224_out);
  nand nand_261 (nand_261_out, nand_225_out, nand_225_out);
  nand nand_262 (nand_262_out, nand_226_out, nand_227_out);
  nand nand_263 (nand_263_out, nand_228_out, nand_229_out);
  nand nand_264 (nand_264_out, nand_230_out, nand_231_out);
  nand nand_265 (nand_265_out, nand_232_out, nand_232_out);
  nand nand_266 (nand_266_out, nand_233_out, nand_234_out);
  nand nand_267 (nand_267_out, nand_235_out, nand_236_out);
  nand nand_268 (nand_268_out, nand_237_out, nand_238_out);
  nand nand_269 (nand_269_out, nand_239_out, nand_239_out);
  nand nand_270 (nand_270_out, nand_240_out, nand_240_out);
  nand nand_271 (nand_271_out, nand_241_out, nand_241_out);
  nand nand_272 (nand_272_out, nand_242_out, nand_242_out);
  nand nand_273 (nand_273_out, nand_243_out, nand_243_out);
  nand nand_274 (nand_274_out, nand_244_out, nand_244_out);
  nand nand_275 (nand_275_out, nand_245_out, nand_246_out);
  nand nand_276 (nand_276_out, nand_247_out, nand_247_out);
  nand nand_277 (nand_277_out, nand_248_out, nand_248_out);
  nand nand_278 (nand_278_out, nand_249_out, nand_250_out);
  nand nand_279 (nand_279_out, nand_251_out, nand_251_out);
  nand nand_280 (nand_280_out, nand_252_out, nand_252_out);
  nand nand_281 (nand_281_out, nand_253_out, nand_254_out);
  nand nand_282 (nand_282_out, nand_255_out, nand_256_out);
  nand nand_283 (nand_283_out, nand_257_out, nand_258_out);
  nand nand_284 (nand_284_out, nand_259_out, nand_260_out);
  nand nand_285 (nand_285_out, nand_261_out, nand_262_out);
  nand nand_286 (nand_286_out, nand_263_out, nand_264_out);
  nand nand_287 (nand_287_out, nand_265_out, nand_266_out);
  nand nand_288 (nand_288_out, nand_267_out, nand_268_out);
  nand nand_289 (O_1[1], nand_269_out, nand_270_out);
  nand nand_290 (nand_290_out, nand_271_out, nand_272_out);
  nand nand_291 (nand_291_out, nand_273_out, nand_274_out);
  nand nand_292 (nand_292_out, nand_275_out, nand_275_out);
  nand nand_293 (nand_293_out, nand_276_out, nand_277_out);
  nand nand_294 (nand_294_out, nand_278_out, nand_278_out);
  nand nand_295 (nand_295_out, nand_279_out, nand_280_out);
  nand nand_296 (nand_296_out, nand_281_out, nand_281_out);
  nand nand_297 (nand_297_out, nand_282_out, nand_282_out);
  nand nand_298 (nand_298_out, nand_283_out, nand_283_out);
  nand nand_299 (nand_299_out, nand_284_out, nand_284_out);
  nand nand_300 (nand_300_out, nand_285_out, nand_285_out);
  nand nand_301 (nand_301_out, nand_286_out, nand_286_out);
  nand nand_302 (nand_302_out, nand_287_out, nand_287_out);
  nand nand_303 (nand_303_out, nand_288_out, nand_288_out);
  nand nand_304 (nand_304_out, nand_290_out, nand_290_out);
  nand nand_305 (nand_305_out, nand_291_out, nand_291_out);
  nand nand_306 (nand_306_out, nand_292_out, nand_293_out);
  nand nand_307 (nand_307_out, nand_294_out, nand_295_out);
  nand nand_308 (nand_308_out, nand_296_out, nand_297_out);
  nand nand_309 (nand_309_out, nand_298_out, nand_299_out);
  nand nand_310 (nand_310_out, nand_300_out, nand_301_out);
  nand nand_311 (nand_311_out, nand_302_out, nand_303_out);
  nand nand_312 (O_1[0], nand_304_out, nand_305_out);
  nand nand_313 (nand_313_out, nand_306_out, nand_306_out);
  nand nand_314 (nand_314_out, nand_307_out, nand_307_out);
  nand nand_315 (nand_315_out, nand_308_out, nand_308_out);
  nand nand_316 (nand_316_out, nand_309_out, nand_309_out);
  nand nand_317 (nand_317_out, nand_310_out, nand_310_out);
  nand nand_318 (nand_318_out, nand_311_out, nand_311_out);
  nand nand_319 (O_0[3], nand_313_out, nand_314_out);
  nand nand_320 (O_0[2], nand_315_out, nand_316_out);
  nand nand_321 (O_0[1], nand_317_out, nand_318_out);

  assign {O_0[4], O_0[0]} = {1'b0, t_in[0]};
  assign O_1[4:3] = 2'b00;
endmodule

module binary_to_time_converter (
  input  [4:0] Input_bus_1,
  input  [4:0] Input_bus_2,
  output [5:0] Output_bus_1
);

  wire nand_1_out, nand_2_out, nand_3_out, nand_4_out, nand_5_out, nand_6_out, nand_7_out, nand_8_out,
       nand_9_out, nand_10_out, nand_11_out, nand_12_out, nand_13_out, nand_14_out, nand_15_out, nand_16_out,
       nand_17_out, nand_18_out, nand_19_out, nand_20_out, nand_21_out, nand_22_out, nand_23_out,
       nand_24_out, nand_25_out, nand_26_out, nand_27_out, nand_28_out, nand_29_out, nand_30_out,
       nand_31_out, nand_32_out, nand_33_out, nand_34_out, nand_35_out, nand_36_out, nand_37_out,
       nand_38_out, nand_39_out, nand_40_out, nand_41_out, nand_42_out, nand_43_out, nand_44_out,
       nand_45_out, nand_46_out, nand_47_out, nand_48_out, nand_49_out, nand_50_out, nand_51_out,
       nand_52_out, nand_53_out, nand_54_out, nand_55_out, nand_56_out, nand_57_out, nand_58_out,
       nand_59_out, nand_60_out, nand_61_out, nand_62_out, nand_63_out, nand_64_out, nand_65_out,
       nand_66_out, nand_67_out, nand_68_out, nand_69_out, nand_71_out, nand_72_out, nand_73_out,
       nand_74_out, nand_75_out, nand_76_out, nand_77_out, nand_78_out, nand_79_out, nand_80_out,
       nand_81_out, nand_82_out, nand_83_out, nand_84_out, nand_85_out, nand_86_out, nand_87_out,
       nand_88_out, nand_89_out, nand_90_out, nand_91_out, nand_92_out, nand_93_out, nand_94_out,
       nand_95_out, nand_96_out, nand_97_out, nand_98_out, nand_99_out, nand_100_out, nand_101_out,
       nand_102_out, nand_103_out, nand_104_out, nand_105_out, nand_106_out, nand_107_out, nand_108_out,
       nand_109_out, nand_110_out, nand_111_out, nand_112_out, nand_113_out, nand_114_out, nand_115_out,
       nand_116_out, nand_117_out, nand_118_out, nand_119_out, nand_120_out, nand_121_out, nand_122_out,
       nand_123_out, nand_124_out, nand_126_out, nand_127_out, nand_128_out, nand_129_out, nand_130_out,
       nand_131_out, nand_132_out, nand_133_out, nand_134_out, nand_135_out, nand_136_out, nand_137_out,
       nand_138_out, nand_139_out, nand_140_out, nand_141_out, nand_142_out, nand_143_out, nand_144_out,
       nand_145_out, nand_146_out, nand_147_out, nand_148_out, nand_149_out, nand_150_out, nand_151_out,
       nand_152_out, nand_153_out, nand_154_out, nand_155_out, nand_156_out, nand_157_out, nand_158_out,
       nand_159_out, nand_160_out, nand_161_out, nand_162_out, nand_163_out, nand_164_out, nand_165_out,
       nand_168_out, nand_169_out, nand_171_out, nand_172_out;

  nand nand_1 (nand_1_out, Input_bus_2[2], Input_bus_2[2]);
  nand nand_2 (nand_2_out, Input_bus_2[0], Input_bus_2[0]);
  nand nand_3 (nand_3_out, Input_bus_1[1], Input_bus_1[1]);
  nand nand_4 (nand_4_out, Input_bus_1[1], Input_bus_1[1]);
  nand nand_5 (nand_5_out, Input_bus_2[3], Input_bus_2[3]);
  nand nand_6 (nand_6_out, Input_bus_2[2], Input_bus_2[2]);
  nand nand_7 (nand_7_out, Input_bus_2[1], Input_bus_2[1]);
  nand nand_8 (nand_8_out, Input_bus_1[2], Input_bus_1[2]);
  nand nand_9 (nand_9_out, Input_bus_1[1], Input_bus_1[1]);
  nand nand_10 (nand_10_out, Input_bus_1[2], Input_bus_1[2]);
  nand nand_11 (nand_11_out, Input_bus_1[1], Input_bus_1[1]);
  nand nand_12 (nand_12_out, Input_bus_1[2], Input_bus_1[2]);
  nand nand_13 (nand_13_out, Input_bus_1[1], Input_bus_1[1]);
  nand nand_14 (nand_14_out, Input_bus_1[0], Input_bus_1[0]);
  nand nand_15 (nand_15_out, Input_bus_1[1], Input_bus_1[1]);
  nand nand_16 (nand_16_out, Input_bus_1[0], Input_bus_1[0]);
  nand nand_17 (nand_17_out, Input_bus_2[2], Input_bus_2[2]);
  nand nand_18 (nand_18_out, Input_bus_1[0], Input_bus_1[0]);
  nand nand_19 (nand_19_out, Input_bus_2[1], Input_bus_2[1]);
  nand nand_20 (nand_20_out, Input_bus_2[2], Input_bus_2[2]);
  nand nand_21 (nand_21_out, Input_bus_2[3], nand_1_out);
  nand nand_22 (nand_22_out, Input_bus_2[1], nand_2_out);
  nand nand_23 (nand_23_out, Input_bus_1[1], Input_bus_1[0]);
  nand nand_24 (nand_24_out, nand_3_out, Input_bus_1[0]);
  nand nand_25 (nand_25_out, Input_bus_2[2], Input_bus_2[1]);
  nand nand_26 (nand_26_out, nand_4_out, Input_bus_1[0]);
  nand nand_27 (nand_27_out, Input_bus_1[1], nand_5_out);
  nand nand_28 (nand_28_out, nand_6_out, nand_7_out);
  nand nand_29 (nand_29_out, nand_8_out, nand_9_out);
  nand nand_30 (nand_30_out, nand_10_out, nand_11_out);
  nand nand_31 (nand_31_out, nand_12_out, Input_bus_1[0]);
  nand nand_32 (nand_32_out, nand_13_out, nand_14_out);
  nand nand_33 (nand_33_out, nand_15_out, Input_bus_2[2]);
  nand nand_34 (nand_34_out, Input_bus_1[1], nand_16_out);
  nand nand_35 (nand_35_out, Input_bus_1[1], nand_17_out);
  nand nand_36 (nand_36_out, nand_18_out, Input_bus_2[1]);
  nand nand_37 (nand_37_out, Input_bus_1[0], nand_19_out);
  nand nand_38 (nand_38_out, Input_bus_2[3], nand_20_out);
  nand nand_39 (nand_39_out, nand_21_out, nand_21_out);
  nand nand_40 (nand_40_out, nand_22_out, nand_22_out);
  nand nand_41 (nand_41_out, nand_23_out, nand_23_out);
  nand nand_42 (nand_42_out, nand_24_out, nand_24_out);
  nand nand_43 (nand_43_out, nand_25_out, nand_25_out);
  nand nand_44 (nand_44_out, nand_26_out, nand_26_out);
  nand nand_45 (nand_45_out, nand_27_out, nand_27_out);
  nand nand_46 (nand_46_out, nand_28_out, nand_28_out);
  nand nand_47 (nand_47_out, Input_bus_1[2], Input_bus_1[2]);
  nand nand_48 (nand_48_out, Input_bus_1[0], Input_bus_1[0]);
  nand nand_49 (nand_49_out, nand_29_out, nand_29_out);
  nand nand_50 (nand_50_out, Input_bus_2[3], Input_bus_2[3]);
  nand nand_51 (nand_51_out, Input_bus_2[2], Input_bus_2[2]);
  nand nand_52 (nand_52_out, nand_30_out, nand_30_out);
  nand nand_53 (nand_53_out, Input_bus_2[3], Input_bus_2[3]);
  nand nand_54 (nand_54_out, Input_bus_2[1], Input_bus_2[1]);
  nand nand_55 (nand_55_out, nand_31_out, nand_31_out);
  nand nand_56 (nand_56_out, Input_bus_2[3], Input_bus_2[3]);
  nand nand_57 (nand_57_out, Input_bus_2[2], Input_bus_2[2]);
  nand nand_58 (nand_58_out, Input_bus_2[1], Input_bus_2[1]);
  nand nand_59 (nand_59_out, Input_bus_1[0], Input_bus_1[0]);
  nand nand_60 (nand_60_out, Input_bus_1[0], Input_bus_1[0]);
  nand nand_61 (nand_61_out, nand_32_out, nand_32_out);
  nand nand_62 (nand_62_out, nand_33_out, nand_33_out);
  nand nand_63 (nand_63_out, Input_bus_2[1], Input_bus_2[1]);
  nand nand_64 (nand_64_out, Input_bus_1[1], Input_bus_1[1]);
  nand nand_65 (nand_65_out, Input_bus_2[2], Input_bus_2[2]);
  nand nand_66 (nand_66_out, nand_34_out, nand_34_out);
  nand nand_67 (nand_67_out, Input_bus_2[2], Input_bus_2[2]);
  nand nand_68 (nand_68_out, nand_35_out, nand_35_out);
  nand nand_69 (nand_69_out, Input_bus_2[1], Input_bus_2[1]);
  nand nand_70 (Output_bus_1[1], nand_36_out, nand_37_out);
  nand nand_71 (nand_71_out, nand_38_out, nand_38_out);
  nand nand_72 (nand_72_out, nand_39_out, nand_40_out);
  nand nand_73 (nand_73_out, nand_41_out, Input_bus_2[1]);
  nand nand_74 (nand_74_out, Input_bus_1[1], Input_bus_1[0]);
  nand nand_75 (nand_75_out, Input_bus_1[1], Input_bus_1[0]);
  nand nand_76 (nand_76_out, nand_42_out, nand_43_out);
  nand nand_77 (nand_77_out, nand_44_out, Input_bus_2[3]);
  nand nand_78 (nand_78_out, nand_45_out, nand_46_out);
  nand nand_79 (nand_79_out, Input_bus_1[2], Input_bus_2[3]);
  nand nand_80 (nand_80_out, nand_47_out, nand_48_out);
  nand nand_81 (nand_81_out, nand_49_out, Input_bus_1[0]);
  nand nand_82 (nand_82_out, nand_50_out, nand_51_out);
  nand nand_83 (nand_83_out, nand_52_out, Input_bus_1[0]);
  nand nand_84 (nand_84_out, nand_53_out, nand_54_out);
  nand nand_85 (nand_85_out, nand_55_out, nand_56_out);
  nand nand_86 (nand_86_out, nand_57_out, nand_58_out);
  nand nand_87 (nand_87_out, Input_bus_1[1], nand_59_out);
  nand nand_88 (nand_88_out, Input_bus_1[2], nand_60_out);
  nand nand_89 (nand_89_out, Input_bus_1[2], Input_bus_2[2]);
  nand nand_90 (nand_90_out, Input_bus_1[2], Input_bus_1[0]);
  nand nand_91 (nand_91_out, nand_61_out, Input_bus_2[2]);
  nand nand_92 (nand_92_out, nand_62_out, nand_63_out);
  nand nand_93 (nand_93_out, nand_64_out, Input_bus_1[0]);
  nand nand_94 (nand_94_out, nand_65_out, Input_bus_2[1]);
  nand nand_95 (nand_95_out, nand_66_out, nand_67_out);
  nand nand_96 (nand_96_out, nand_68_out, nand_69_out);
  nand nand_97 (nand_97_out, Input_bus_1[1], Input_bus_1[0]);
  nand nand_98 (nand_98_out, Input_bus_2[2], Input_bus_2[1]);
  nand nand_99 (nand_99_out, Input_bus_2[0], Input_bus_2[0]);
  nand nand_100 (nand_100_out, nand_71_out, Input_bus_2[1]);
  nand nand_101 (nand_101_out, nand_72_out, nand_73_out);
  nand nand_102 (nand_102_out, nand_74_out, nand_74_out);
  nand nand_103 (nand_103_out, nand_75_out, nand_75_out);
  nand nand_104 (nand_104_out, nand_76_out, nand_77_out);
  nand nand_105 (nand_105_out, Input_bus_1[0], Input_bus_1[0]);
  nand nand_106 (nand_106_out, nand_78_out, nand_79_out);
  nand nand_107 (nand_107_out, nand_80_out, nand_80_out);
  nand nand_108 (nand_108_out, nand_81_out, nand_81_out);
  nand nand_109 (nand_109_out, nand_82_out, nand_82_out);
  nand nand_110 (nand_110_out, nand_83_out, nand_83_out);
  nand nand_111 (nand_111_out, nand_84_out, nand_84_out);
  nand nand_112 (nand_112_out, nand_85_out, nand_85_out);
  nand nand_113 (nand_113_out, nand_86_out, nand_86_out);
  nand nand_114 (nand_114_out, nand_87_out, nand_87_out);
  nand nand_115 (nand_115_out, nand_88_out, nand_88_out);
  nand nand_116 (nand_116_out, Input_bus_2[3], Input_bus_2[3]);
  nand nand_117 (nand_117_out, nand_89_out, nand_89_out);
  nand nand_118 (nand_118_out, nand_90_out, nand_90_out);
  nand nand_119 (nand_119_out, nand_91_out, nand_92_out);
  nand nand_120 (nand_120_out, nand_93_out, nand_93_out);
  nand nand_121 (nand_121_out, nand_94_out, nand_94_out);
  nand nand_122 (nand_122_out, nand_95_out, nand_96_out);
  nand nand_123 (nand_123_out, nand_97_out, nand_97_out);
  nand nand_124 (nand_124_out, nand_98_out, nand_98_out);
  nand nand_125 (Output_bus_1[0], nand_99_out, nand_100_out);
  nand nand_126 (nand_126_out, nand_101_out, nand_101_out);
  nand nand_127 (nand_127_out, nand_102_out, Input_bus_2[2]);
  nand nand_128 (nand_128_out, nand_103_out, Input_bus_2[3]);
  nand nand_129 (nand_129_out, Input_bus_1[2], Input_bus_1[2]);
  nand nand_130 (nand_130_out, nand_104_out, nand_104_out);
  nand nand_131 (nand_131_out, Input_bus_1[1], nand_105_out);
  nand nand_132 (nand_132_out, nand_106_out, nand_106_out);
  nand nand_133 (nand_133_out, Input_bus_1[2], Input_bus_1[0]);
  nand nand_134 (nand_134_out, nand_107_out, Input_bus_2[3]);
  nand nand_135 (nand_135_out, nand_108_out, nand_109_out);
  nand nand_136 (nand_136_out, nand_110_out, nand_111_out);
  nand nand_137 (nand_137_out, nand_112_out, nand_113_out);
  nand nand_138 (nand_138_out, nand_114_out, Input_bus_2[2]);
  nand nand_139 (nand_139_out, nand_115_out, nand_116_out);
  nand nand_140 (nand_140_out, nand_117_out, Input_bus_2[1]);
  nand nand_141 (nand_141_out, nand_118_out, Input_bus_2[3]);
  nand nand_142 (nand_142_out, nand_119_out, nand_119_out);
  nand nand_143 (nand_143_out, nand_120_out, nand_121_out);
  nand nand_144 (nand_144_out, nand_122_out, nand_122_out);
  nand nand_145 (nand_145_out, nand_123_out, nand_124_out);
  nand nand_146 (nand_146_out, nand_126_out, nand_127_out);
  nand nand_147 (nand_147_out, nand_128_out, nand_129_out);
  nand nand_148 (nand_148_out, nand_130_out, nand_131_out);
  nand nand_149 (nand_149_out, nand_132_out, nand_133_out);
  nand nand_150 (nand_150_out, nand_134_out, nand_135_out);
  nand nand_151 (nand_151_out, nand_136_out, nand_137_out);
  nand nand_152 (nand_152_out, nand_138_out, nand_139_out);
  nand nand_153 (nand_153_out, nand_140_out, nand_141_out);
  nand nand_154 (nand_154_out, nand_142_out, nand_143_out);
  nand nand_155 (nand_155_out, nand_144_out, nand_145_out);
  nand nand_156 (nand_156_out, nand_146_out, nand_146_out);
  nand nand_157 (nand_157_out, nand_147_out, nand_147_out);
  nand nand_158 (nand_158_out, nand_148_out, nand_148_out);
  nand nand_159 (nand_159_out, nand_149_out, nand_149_out);
  nand nand_160 (nand_160_out, nand_150_out, nand_150_out);
  nand nand_161 (nand_161_out, nand_151_out, nand_151_out);
  nand nand_162 (nand_162_out, nand_152_out, nand_152_out);
  nand nand_163 (nand_163_out, nand_153_out, nand_153_out);
  nand nand_164 (nand_164_out, nand_154_out, nand_154_out);
  nand nand_165 (nand_165_out, nand_155_out, nand_155_out);
  nand nand_166 (Output_bus_1[5], nand_156_out, nand_157_out);
  nand nand_167 (Output_bus_1[4], nand_158_out, nand_159_out);
  nand nand_168 (nand_168_out, nand_160_out, nand_161_out);
  nand nand_169 (nand_169_out, nand_162_out, nand_163_out);
  nand nand_170 (Output_bus_1[2], nand_164_out, nand_165_out);
  nand nand_171 (nand_171_out, nand_168_out, nand_168_out);
  nand nand_172 (nand_172_out, nand_169_out, nand_169_out);
  nand nand_173 (Output_bus_1[3], nand_171_out, nand_172_out);
endmodule

module test (
  input  C_2,
  input  C_1,
  input  C_0,
  input  S_3,
  input  S_2,
  input  S_1,
  input  S_0,
  output O_3,
  output O_2,
  output O_1,
  output O_0
);

  wire and_1_out, and_2_out, and_3_out, and_4_out, and_5_out, and_6_out, and_7_out, and_8_out, and_9_out,
       and_10_out, and_11_out, and_12_out, and_13_out, and_14_out, and_15_out, and_16_out, and_17_out,
       and_18_out, and_19_out, and_20_out, and_21_out, and_22_out, and_23_out, and_24_out, and_25_out,
       and_26_out, and_27_out, and_28_out, and_29_out, and_30_out, and_31_out, and_32_out, and_33_out,
       and_34_out, and_35_out, and_36_out, and_37_out, not_1_out, not_2_out, not_3_out, not_4_out, not_5_out,
       not_6_out, not_7_out, not_8_out, not_9_out, not_10_out, not_11_out, not_12_out, not_13_out,
       not_14_out, not_15_out, not_16_out, not_17_out, not_18_out, not_19_out, not_20_out, not_21_out,
       not_22_out, not_23_out, not_24_out, not_25_out, not_26_out, not_27_out, not_28_out, not_29_out,
       not_30_out, not_31_out, not_32_out, not_33_out, not_34_out, not_35_out, not_36_out, not_37_out,
       not_38_out, not_39_out, not_40_out, not_41_out, not_42_out, not_43_out, not_44_out, not_45_out,
       not_46_out, not_47_out, not_48_out, not_49_out, not_50_out, not_51_out, not_52_out, not_53_out,
       not_54_out, not_55_out, not_56_out, not_57_out, not_58_out, not_59_out, not_60_out, not_61_out,
       not_62_out, not_63_out, not_64_out, not_65_out, not_66_out, not_67_out, not_68_out, not_69_out,
       not_70_out, not_71_out, not_72_out, not_73_out, not_74_out, not_75_out, not_76_out, not_77_out,
       not_78_out, not_79_out, not_80_out, not_81_out, not_82_out, not_83_out, not_84_out, not_85_out,
       not_86_out, not_87_out, not_88_out, not_89_out, not_90_out, not_91_out, not_92_out, not_93_out,
       not_94_out;

  not not_1 (not_1_out, C_2);
  not not_2 (not_2_out, C_1);
  not not_3 (not_3_out, C_0);
  not not_4 (not_4_out, S_2);
  not not_5 (not_5_out, C_1);
  not not_6 (not_6_out, C_0);
  not not_7 (not_7_out, C_1);
  not not_8 (not_8_out, S_3);
  not not_9 (not_9_out, C_2);
  not not_10 (not_10_out, C_1);
  not not_11 (not_11_out, S_3);
  not not_12 (not_12_out, S_1);
  not not_13 (not_13_out, C_1);
  not not_14 (not_14_out, S_3);
  not not_15 (not_15_out, S_0);
  not not_16 (not_16_out, C_1);
  not not_17 (not_17_out, C_0);
  not not_18 (not_18_out, C_2);
  not not_19 (not_19_out, C_0);
  not not_20 (not_20_out, C_1);
  not not_21 (not_21_out, C_0);
  not not_22 (not_22_out, C_2);
  not not_23 (not_23_out, C_1);
  not not_24 (not_24_out, C_2);
  not not_25 (not_25_out, S_0);
  not not_26 (not_26_out, C_1);
  not not_27 (not_27_out, C_0);
  not not_28 (not_28_out, S_0);
  not not_29 (not_29_out, C_1);
  not not_30 (not_30_out, S_3);
  not not_31 (not_31_out, S_2);
  not not_32 (not_32_out, C_1);
  not not_33 (not_33_out, S_3);
  not not_34 (not_34_out, S_0);
  not not_35 (not_35_out, C_2);
  not not_36 (not_36_out, C_1);
  not not_37 (not_37_out, C_0);
  not not_38 (not_38_out, C_2);
  not not_39 (not_39_out, C_2);
  not not_40 (not_40_out, C_1);
  not not_41 (not_41_out, S_2);
  not not_42 (not_42_out, C_2);
  not not_43 (not_43_out, C_0);
  not not_44 (not_44_out, S_3);
  not not_45 (not_45_out, C_2);
  not not_46 (not_46_out, S_3);
  not not_47 (not_47_out, S_2);
  not not_48 (not_48_out, C_2);
  not not_49 (not_49_out, C_1);
  not not_50 (not_50_out, C_0);
  not not_51 (not_51_out, C_2);
  not not_52 (not_52_out, C_0);
  not not_53 (not_53_out, S_2);
  not not_54 (not_54_out, S_1);
  not not_55 (not_55_out, C_1);
  not not_56 (not_56_out, C_0);
  not not_57 (not_57_out, S_2);
  not not_58 (not_58_out, S_1);
  not not_59 (not_59_out, C_1);
  not not_60 (not_60_out, S_3);
  not not_61 (not_61_out, S_2);
  not not_62 (not_62_out, C_1);
  not not_63 (not_63_out, S_3);
  not not_64 (not_64_out, S_1);
  not not_65 (not_65_out, C_2);
  not not_66 (not_66_out, C_1);
  not not_67 (not_67_out, C_0);
  not not_68 (not_68_out, C_2);
  not not_69 (not_69_out, C_1);
  not not_70 (not_70_out, S_3);
  not not_71 (not_71_out, S_2);
  not not_72 (not_72_out, C_2);
  not not_73 (not_73_out, C_2);
  not not_74 (not_74_out, C_2);
  not not_75 (not_75_out, C_0);
  not not_76 (not_76_out, S_3);
  not not_77 (not_77_out, S_2);
  not not_78 (not_78_out, S_1);
  not not_79 (not_79_out, C_2);
  not not_80 (not_80_out, C_0);
  not not_81 (not_81_out, S_2);
  not not_82 (not_82_out, C_2);
  not not_83 (not_83_out, C_0);
  not not_84 (not_84_out, S_1);
  not not_85 (not_85_out, C_2);
  not not_86 (not_86_out, S_2);
  not not_87 (not_87_out, S_1);
  not not_88 (not_88_out, C_1);
  not not_89 (not_89_out, C_0);
  not not_90 (not_90_out, S_3);
  not not_91 (not_91_out, S_1);
  not not_92 (not_92_out, C_1);
  not not_93 (not_93_out, S_3);
  not not_94 (not_94_out, S_0);
  and and_1 (and_1_out, not_1_out, S_3);
  and and_2 (and_2_out, not_2_out, not_3_out, S_3, not_4_out);
  and and_3 (and_3_out, not_5_out, not_6_out, S_3, S_1);
  and and_4 (and_4_out, C_2, not_7_out, C_0, not_8_out, S_2, S_1, S_0);
  and and_5 (and_5_out, not_9_out, S_2);
  and and_6 (and_6_out, not_10_out, not_11_out, S_2, not_12_out);
  and and_7 (and_7_out, not_13_out, not_14_out, S_2, not_15_out);
  and and_8 (and_8_out, not_16_out, not_17_out, S_2, S_1);
  and and_9 (and_9_out, not_18_out, C_1, not_19_out, S_1, S_0);
  and and_10 (and_10_out, C_2, not_20_out, not_21_out, S_3, S_1, S_0);
  and and_11 (and_11_out, not_22_out, not_23_out, S_1);
  and and_12 (and_12_out, not_24_out, S_1, not_25_out);
  and and_13 (and_13_out, not_26_out, not_27_out, S_1, not_28_out);
  and and_14 (and_14_out, not_29_out, not_30_out, not_31_out, S_1);
  and and_15 (and_15_out, not_32_out, not_33_out, S_1, not_34_out);
  and and_16 (and_16_out, not_35_out, S_2, S_1);
  and and_17 (and_17_out, not_36_out, not_37_out, S_2, S_1);
  and and_18 (and_18_out, not_38_out, C_0, S_1);
  and and_19 (and_19_out, not_39_out, not_40_out, C_0, S_3, not_41_out, S_0);
  and and_20 (and_20_out, not_42_out, C_1, not_43_out, not_44_out, S_2);
  and and_21 (and_21_out, not_45_out, C_1, C_0, not_46_out, not_47_out, S_0);
  and and_22 (and_22_out, not_48_out, not_49_out, not_50_out, S_0);
  and and_23 (and_23_out, not_51_out, not_52_out, not_53_out, not_54_out, S_0);
  and and_24 (and_24_out, not_55_out, not_56_out, not_57_out, not_58_out, S_0);
  and and_25 (and_25_out, not_59_out, not_60_out, not_61_out, S_0);
  and and_26 (and_26_out, not_62_out, not_63_out, not_64_out, S_0);
  and and_27 (and_27_out, not_65_out, S_2, S_1, S_0);
  and and_28 (and_28_out, not_66_out, not_67_out, S_2, S_1, S_0);
  and and_29 (and_29_out, not_68_out, not_69_out, C_0, not_70_out, not_71_out, S_1);
  and and_30 (and_30_out, not_72_out, C_0, S_1, S_0);
  and and_31 (and_31_out, not_73_out, C_0, S_2, S_0);
  and and_32 (and_32_out, not_74_out, C_1, not_75_out, not_76_out, not_77_out, not_78_out);
  and and_33 (and_33_out, not_79_out, C_1, not_80_out, S_3, not_81_out, S_1);
  and and_34 (and_34_out, not_82_out, C_1, not_83_out, S_3, S_2, not_84_out);
  and and_35 (and_35_out, not_85_out, C_1, C_0, S_3, not_86_out, not_87_out);
  and and_36 (and_36_out, C_2, not_88_out, not_89_out, not_90_out, S_2, not_91_out);
  and and_37 (and_37_out, C_2, not_92_out, C_0, not_93_out, S_2, S_1, not_94_out);
  or or_1 (O_3, and_1_out, and_2_out, and_3_out, and_4_out);
  or or_2 (O_2, and_5_out, and_6_out, and_7_out, and_8_out, and_9_out, and_10_out);
  or or_3 (O_1, and_11_out, and_12_out, and_13_out, and_14_out, and_15_out, and_16_out, and_17_out, and_18_out, and_19_out, and_20_out, and_21_out);
  or or_4 (O_0, and_22_out, and_23_out, and_24_out, and_25_out, and_26_out, and_27_out, and_28_out, and_29_out, and_30_out, and_31_out, and_32_out, and_33_out, and_34_out, and_35_out, and_36_out, and_37_out);
endmodule

module memory_alarm (
  input  [5:0] hour_in,
  input  [5:0] min_in,
  input  [5:0] sec_in,
  input  set,
  input  reset,
  input  enable,
  output [5:0] hour,
  output [5:0] min,
  output [5:0] seconds
);

  Register #(.width(6)) register_1 (.D(hour_in), .en(enable), .clk(set), .Q(hour), .clr(reset));
  Register #(.width(6)) register_2 (.D(min_in), .en(enable), .clk(set), .Q(min), .clr(reset));
  Register #(.width(6)) register_3 (.D(sec_in), .en(enable), .clk(set), .Q(seconds), .clr(reset));
endmodule

module musique (
  input  set_on,
  input  [1:0] music,
  output buzzer_0,
  output buzzer_1
);

  wire clock_1_out, clock_2_out, demultiplexer_1_out0, demultiplexer_1_out1, Do4_out, Do5_out, Do6_out,
       DoD4_out, DoD5_out, DoD6_out, Fa4_out, Fa6_out, Fa_out, FaD4_out, FaD5_out, FaD6_out, La4_out,
       La5_out, Mi4_out, Mi6_out, Mi_out, music_givenTheme_1_freq, not_1_out, not_2_out, Re4_out, Re5_out,
       Re6_out, ReD4_out, ReD5_out, ReD6_out, rv230_allegro_1_freq, Si4_out, Si5_out, SiB4_out, SiB5_out,
       Sol4_out, Sol5_out, Sol6_out, SolD4_out, SolD5_out;

  Clock #(.highDuration(61162), .lowDuration(61162)) Do1 ();  // open: out
  Clock #(.highDuration(57720), .lowDuration(57720)) DoD1 ();  // open: out
  Clock #(.highDuration(54481), .lowDuration(54481)) Re1 ();  // open: out
  Clock #(.highDuration(51427), .lowDuration(51427)) ReD1 ();  // open: out
  Clock #(.highDuration(48544), .lowDuration(48544)) Mi1 ();  // open: out
  Clock #(.highDuration(45819), .lowDuration(45819)) Fa1 ();  // open: out
  Clock #(.highDuration(43243), .lowDuration(43243)) FaD1 ();  // open: out
  Clock #(.highDuration(40816), .lowDuration(40816)) Sol1 ();  // open: out
  Clock #(.highDuration(38528), .lowDuration(38528)) SolD1 ();  // open: out
  Clock #(.highDuration(36364), .lowDuration(36364)) La1 ();  // open: out
  Clock #(.highDuration(34323), .lowDuration(268)) SiB1 ();  // open: out
  Clock #(.highDuration(32394), .lowDuration(32394)) Si1 ();  // open: out
  Clock #(.highDuration(30576), .lowDuration(30576)) Do2 ();  // open: out
  Clock #(.highDuration(28860), .lowDuration(28860)) DoD2 ();  // open: out
  Clock #(.highDuration(27241), .lowDuration(27241)) Re2 ();  // open: out
  Clock #(.highDuration(25714), .lowDuration(25714)) ReD2 ();  // open: out
  Clock #(.highDuration(24269), .lowDuration(24269)) Mi2 ();  // open: out
  Clock #(.highDuration(22907), .lowDuration(284)) Fa2 ();  // open: out
  Clock #(.highDuration(21622), .lowDuration(21622)) FaD2 ();  // open: out
  Clock #(.highDuration(20408), .lowDuration(20408)) Sol2 ();  // open: out
  Clock #(.highDuration(19262), .lowDuration(19262)) SolD2 ();  // open: out
  Clock #(.highDuration(18182), .lowDuration(18182)) La2 ();  // open: out
  Clock #(.highDuration(17161), .lowDuration(17161)) SiB2 ();  // open: out
  Clock #(.highDuration(16198), .lowDuration(16198)) Si2 ();  // open: out
  Clock #(.highDuration(15289), .lowDuration(15289)) Do3 ();  // open: out
  Clock #(.highDuration(14431), .lowDuration(14431)) DoD3 ();  // open: out
  Clock #(.highDuration(13621), .lowDuration(13621)) Re3 ();  // open: out
  Clock #(.highDuration(12857), .lowDuration(12857)) ReD3 ();  // open: out
  Clock #(.highDuration(12135)) Mi3 ();  // open: out
  Clock #(.highDuration(11454), .lowDuration(11454)) Fa3 ();  // open: out
  Clock #(.highDuration(10811), .lowDuration(268)) FaD3 ();  // open: out
  Clock #(.highDuration(10204), .lowDuration(10204)) Sol3 ();  // open: out
  Clock #(.highDuration(9632), .lowDuration(9632)) SolD3 ();  // open: out
  Clock #(.highDuration(9091), .lowDuration(9091)) La3 ();  // open: out
  Clock #(.highDuration(8581), .lowDuration(8581)) SiB3 ();  // open: out
  Clock #(.highDuration(8099), .lowDuration(8099)) Si3 ();  // open: out
  Clock #(.highDuration(3822), .lowDuration(3822)) Do4 (.out(Do4_out));
  Clock #(.highDuration(3608), .lowDuration(3608)) DoD4 (.out(DoD4_out));
  Clock #(.highDuration(3405), .lowDuration(3405)) Re4 (.out(Re4_out));
  Clock #(.highDuration(3214), .lowDuration(3214)) ReD4 (.out(ReD4_out));
  Clock #(.highDuration(3034), .lowDuration(3034)) Mi4 (.out(Mi4_out));
  Clock #(.highDuration(2863), .lowDuration(2863)) Fa4 (.out(Fa4_out));
  Clock #(.highDuration(2703), .lowDuration(2703)) FaD4 (.out(FaD4_out));
  Clock #(.highDuration(2551), .lowDuration(2551)) Sol4 (.out(Sol4_out));
  Clock #(.highDuration(2408), .lowDuration(2408)) SolD4 (.out(SolD4_out));
  Clock #(.highDuration(2273), .lowDuration(2273)) La4 (.out(La4_out));
  Clock #(.highDuration(2145), .lowDuration(2145)) SiB4 (.out(SiB4_out));
  Clock #(.highDuration(2025), .lowDuration(2025)) Si4 (.out(Si4_out));
  Clock #(.highDuration(1911), .lowDuration(1911)) Do5 (.out(Do5_out));
  Clock #(.highDuration(1804), .lowDuration(1804)) DoD5 (.out(DoD5_out));
  Clock #(.highDuration(1703), .lowDuration(1703)) Re5 (.out(Re5_out));
  Clock #(.highDuration(1607), .lowDuration(1607)) ReD5 (.out(ReD5_out));
  Clock #(.highDuration(1517), .lowDuration(1517)) Mi (.out(Mi_out));
  Clock #(.highDuration(1432), .lowDuration(1432)) Fa (.out(Fa_out));
  Clock #(.highDuration(1351), .lowDuration(1351)) FaD5 (.out(FaD5_out));
  Clock #(.highDuration(1276), .lowDuration(1276)) Sol5 (.out(Sol5_out));
  Clock #(.highDuration(1204), .lowDuration(1204)) SolD5 (.out(SolD5_out));
  Clock #(.highDuration(1136), .lowDuration(1136)) La5 (.out(La5_out));
  Clock #(.highDuration(1073), .lowDuration(1073)) SiB5 (.out(SiB5_out));
  Clock #(.highDuration(1012), .lowDuration(1012)) Si5 (.out(Si5_out));
  Clock #(.highDuration(956), .lowDuration(956)) Do6 (.out(Do6_out));
  Clock #(.highDuration(902), .lowDuration(902)) DoD6 (.out(DoD6_out));
  Clock #(.highDuration(851), .lowDuration(851)) Re6 (.out(Re6_out));
  Clock #(.highDuration(804), .lowDuration(804)) ReD6 (.out(ReD6_out));
  Clock #(.highDuration(758), .lowDuration(758)) Mi6 (.out(Mi6_out));
  Clock #(.highDuration(716), .lowDuration(716)) Fa6 (.out(Fa6_out));
  Clock #(.highDuration(676), .lowDuration(676)) FaD6 (.out(FaD6_out));
  Clock #(.highDuration(638), .lowDuration(638)) Sol6 (.out(Sol6_out));
  Clock #(.highDuration(1204), .lowDuration(1204)) SolD6 ();  // open: out
  Clock #(.highDuration(1136), .lowDuration(1136)) La6 ();  // open: out
  Clock #(.highDuration(1073), .lowDuration(1073)) Sib6 ();  // open: out
  Clock #(.highDuration(1012), .lowDuration(1012)) Si6 ();  // open: out
  Clock #(.highDuration(956), .lowDuration(956)) Do7 ();  // open: out
  Clock #(.highDuration(902), .lowDuration(902)) DoD7 ();  // open: out
  Clock #(.highDuration(851), .lowDuration(851)) Re7 ();  // open: out
  Clock #(.highDuration(804), .lowDuration(804)) ReD7 ();  // open: out
  Clock #(.highDuration(758), .lowDuration(758)) Mi7 ();  // open: out
  Clock #(.highDuration(716), .lowDuration(716)) Fa7 ();  // open: out
  Clock #(.highDuration(676), .lowDuration(676)) FaD7 ();  // open: out
  Clock #(.highDuration(638), .lowDuration(638)) Sol7 ();  // open: out
  Clock #(.highDuration(602), .lowDuration(602)) SolD7 ();  // open: out
  Clock #(.highDuration(568), .lowDuration(568)) La7 ();  // open: out
  Clock #(.highDuration(536), .lowDuration(536)) SiB7 ();  // open: out
  Clock #(.highDuration(506), .lowDuration(506)) Si7 ();  // open: out
  Clock #(.highDuration(478), .lowDuration(478)) Do8 ();  // open: out
  Clock #(.highDuration(451), .lowDuration(451)) DoD8 ();  // open: out
  Clock #(.highDuration(426), .lowDuration(426)) Re8 ();  // open: out
  Clock #(.highDuration(402), .lowDuration(402)) ReD8 ();  // open: out
  Clock #(.highDuration(379), .lowDuration(379)) Mi8 ();  // open: out
  Clock #(.highDuration(358), .lowDuration(358)) Fa8 ();  // open: out
  Clock #(.highDuration(338), .lowDuration(338)) FaD8 ();  // open: out
  Clock #(.highDuration(319), .lowDuration(319)) Sol8 ();  // open: out
  Clock #(.highDuration(301), .lowDuration(301)) SolD8 ();  // open: out
  Clock #(.highDuration(284), .lowDuration(284)) La8 ();  // open: out
  Clock #(.highDuration(268), .lowDuration(268)) SiB8 ();  // open: out
  Clock #(.highDuration(253), .lowDuration(253)) Si8 ();  // open: out
  Demultiplexer #(.select(2), .enable("false")) demultiplexer_1 (
    .out0(demultiplexer_1_out0), .out1(demultiplexer_1_out1), .in(set_on), .sel(music));  // open: out2, out3
  Clock #(.highDuration(400000), .lowDuration(400000)) clock_1 (.out(clock_1_out));
  Clock #(.highDuration(400000), .lowDuration(400000)) clock_2 (.out(clock_2_out));
  not not_1 (not_1_out, demultiplexer_1_out0);
  not not_2 (not_2_out, demultiplexer_1_out1);
  music_givenTheme music_givenTheme_1 (
    .set_on(demultiplexer_1_out0), .Ds(ReD4_out), .E(Mi4_out), .F(Fa4_out), .Fs(FaD4_out), .G(Sol4_out),
    .B(Si4_out), .A2(La5_out), .B2(Si5_out), .reset(not_1_out), .music_clock(clock_1_out),
    .freq(music_givenTheme_1_freq));
  RV230_allegro rv230_allegro_1 (
    .set_on(demultiplexer_1_out1), .La(La4_out), .Si(Si4_out), .DoD2(DoD5_out), .Re2(Re5_out), .Mi2(Mi_out),
    .FaD2(FaD5_out), .Sol22(Sol5_out), .La2(La5_out), .Si2(Si5_out), .Soupir(1'b0), .reset(not_2_out),
    .music_clock(clock_2_out), .freq(rv230_allegro_1_freq));
  Multiplexer #(.select(2), .enable("false")) multiplexer_1 (
    .in0(music_givenTheme_1_freq), .in1(rv230_allegro_1_freq), .out(buzzer_1), .sel(music));  // open: in2, in3

  assign buzzer_0 = 1'b0;
endmodule

module music_givenTheme (
  input  set_on,
  input  Ds,
  input  E,
  input  F,
  input  Fs,
  input  G,
  input  B,
  input  A2,
  input  B2,
  input  reset,
  input  music_clock,
  output freq
);

  wire clock_1_out, multiplexer_1_out, music_givenTheme_logic_1_o_0, music_givenTheme_logic_1_o_1,
       music_givenTheme_logic_1_o_2, music_givenTheme_logic_1_o_3, not_1_out, not_2_out, not_3_out,
       not_4_out, or_1_out, shift_register_1_p2, shift_register_1_p3;
  wire [2:0] counter_1_q;
  wire [3:0] s_r_ff_4_q;

  Clock clock_1 (.out(clock_1_out));
  Counter #(.width(3), .max('h7)) counter_1 (
    .clr(or_1_out), .load(1'b0), .up(1'b1), .count(1'b1), .clk(music_clock), .D(3'b000), .Q(counter_1_q));  // open: carry
  or or_1 (or_1_out, reset, shift_register_1_p3);
  Multiplexer #(.select(4), .enable("false")) multiplexer_1 (
    .in0(B), .in1(E), .in2(G), .in3(F), .in4(E), .in5(B2), .in6(A2), .in7(Fs), .in8(E), .in9(G), .in10(F),
    .in11(Ds), .in12(F), .in13(B), .out(multiplexer_1_out), .sel(s_r_ff_4_q));  // open: in14, in15
  and and_1 (freq, set_on, multiplexer_1_out);
  // Probe on s_r_ff_4_q
  // Shift_Register #(.length(1)) shift_register_1: pin names not known; wires that end beside it: clock_1_out, shift_register_1_p2, shift_register_1_p3
  music_givenTheme_logic music_givenTheme_logic_1 (
    .C_2(counter_1_q[2]), .C_1(counter_1_q[1]), .C_0(counter_1_q[0]), .S_3(s_r_ff_4_q[3]),
    .S_2(s_r_ff_4_q[2]), .S_1(s_r_ff_4_q[1]), .S_0(s_r_ff_4_q[0]), .O_3(music_givenTheme_logic_1_o_3),
    .O_2(music_givenTheme_logic_1_o_2), .O_1(music_givenTheme_logic_1_o_1),
    .O_0(music_givenTheme_logic_1_o_0), .reset(shift_register_1_p2));
  S_R_Flip_Flop s_r_ff_1 (
    .S(music_givenTheme_logic_1_o_3), .R(not_1_out), .clk(clock_1_out), .Q(s_r_ff_4_q[3]), .reset(reset));  // open: Qn, preset
  not not_1 (not_1_out, music_givenTheme_logic_1_o_3);
  S_R_Flip_Flop s_r_ff_2 (
    .S(music_givenTheme_logic_1_o_2), .R(not_2_out), .clk(clock_1_out), .Q(s_r_ff_4_q[2]), .reset(reset));  // open: Qn, preset
  not not_2 (not_2_out, music_givenTheme_logic_1_o_2);
  S_R_Flip_Flop s_r_ff_3 (
    .S(music_givenTheme_logic_1_o_1), .R(not_3_out), .clk(clock_1_out), .Q(s_r_ff_4_q[1]), .reset(reset));  // open: Qn, preset
  not not_3 (not_3_out, music_givenTheme_logic_1_o_1);
  S_R_Flip_Flop s_r_ff_4 (
    .S(music_givenTheme_logic_1_o_0), .R(not_4_out), .clk(clock_1_out), .Q(s_r_ff_4_q[0]), .reset(reset));  // open: Qn, preset
  not not_4 (not_4_out, music_givenTheme_logic_1_o_0);
endmodule
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module set_time_zone_logic (
  input  old_state_2,
  input  old_state_1,
  input  old_state_0,
  input  in_pressed,
  input  mode_on,
  output sign,
  output value_5,
  output value_4,
  output value_3,
  output value_2,
  output value_1,
  output value_0,
  output S_2,
  output S_1,
  output S_0
);

  wire nand_1_out, nand_2_out, nand_3_out, nand_4_out, nand_5_out, nand_6_out, nand_7_out, nand_8_out,
       nand_9_out, nand_10_out, nand_11_out, nand_12_out, nand_13_out, nand_14_out, nand_15_out, nand_16_out,
       nand_17_out, nand_18_out, nand_19_out, nand_20_out, nand_21_out, nand_22_out, nand_23_out,
       nand_24_out, nand_25_out, nand_26_out, nand_27_out, nand_28_out, nand_29_out, nand_30_out,
       nand_31_out, nand_32_out, nand_33_out, nand_34_out, nand_35_out, nand_36_out, nand_37_out,
       nand_38_out, nand_39_out, nand_40_out, nand_41_out, nand_42_out, nand_43_out, nand_44_out,
       nand_45_out, nand_46_out, nand_47_out, nand_48_out, nand_49_out, nand_50_out, nand_51_out,
       nand_52_out, nand_53_out, nand_54_out, nand_55_out, nand_56_out, nand_57_out, nand_58_out,
       nand_59_out, nand_60_out, nand_61_out, nand_62_out, nand_63_out, nand_64_out, nand_65_out,
       nand_66_out, nand_67_out, nand_68_out, nand_69_out, nand_70_out, nand_71_out, nand_72_out,
       nand_73_out, nand_74_out, nand_75_out, nand_76_out, nand_77_out, nand_78_out, nand_79_out,
       nand_80_out, nand_81_out, nand_82_out, nand_83_out, nand_84_out, nand_85_out, nand_86_out,
       nand_87_out, nand_88_out, nand_89_out, nand_90_out, nand_91_out, nand_92_out, nand_93_out,
       nand_94_out, nand_95_out, nand_96_out, nand_97_out, nand_98_out, nand_99_out, nand_100_out,
       nand_101_out, nand_102_out, nand_103_out, nand_104_out, nand_105_out, nand_106_out, nand_107_out,
       nand_108_out, nand_109_out, nand_110_out, nand_111_out, nand_112_out, nand_113_out, nand_114_out,
       nand_115_out, nand_116_out, nand_118_out, nand_119_out, nand_120_out, nand_121_out, nand_122_out,
       nand_123_out, nand_124_out, nand_125_out, nand_126_out, nand_127_out, nand_128_out, nand_129_out,
       nand_130_out, nand_131_out, nand_132_out, nand_133_out, nand_134_out, nand_135_out, nand_136_out,
       nand_137_out, nand_138_out, nand_139_out, nand_140_out, nand_141_out, nand_142_out, nand_143_out,
       nand_144_out, nand_145_out, nand_146_out, nand_147_out, nand_148_out, nand_149_out, nand_150_out,
       nand_151_out, nand_152_out, nand_153_out, nand_154_out, nand_155_out, nand_156_out, nand_157_out,
       nand_158_out, nand_159_out, nand_160_out, nand_161_out, nand_162_out, nand_163_out, nand_164_out,
       nand_165_out, nand_166_out, nand_167_out, nand_168_out, nand_169_out, nand_170_out, nand_174_out,
       nand_175_out, nand_176_out, nand_177_out, nand_178_out, nand_179_out, nand_181_out, nand_182_out,
       nand_183_out, nand_184_out, nand_185_out, nand_186_out, nand_187_out, nand_188_out;

  nand nand_1 (nand_1_out, old_state_2, old_state_2);
  nand nand_2 (nand_2_out, old_state_1, old_state_1);
  nand nand_3 (nand_3_out, old_state_1, old_state_1);
  nand nand_4 (nand_4_out, old_state_0, old_state_0);
  nand nand_5 (nand_5_out, mode_on, mode_on);
  nand nand_6 (nand_6_out, old_state_2, old_state_2);
  nand nand_7 (nand_7_out, old_state_1, old_state_1);
  nand nand_8 (nand_8_out, old_state_1, old_state_1);
  nand nand_9 (nand_9_out, old_state_2, old_state_2);
  nand nand_10 (nand_10_out, old_state_0, old_state_0);
  nand nand_11 (nand_11_out, old_state_1, old_state_1);
  nand nand_12 (nand_12_out, old_state_2, old_state_2);
  nand nand_13 (nand_13_out, old_state_0, old_state_0);
  nand nand_14 (nand_14_out, old_state_2, old_state_2);
  nand nand_15 (nand_15_out, old_state_1, old_state_1);
  nand nand_16 (nand_16_out, old_state_1, old_state_1);
  nand nand_17 (nand_17_out, old_state_1, old_state_1);
  nand nand_18 (nand_18_out, old_state_2, old_state_2);
  nand nand_19 (nand_19_out, old_state_2, old_state_2);
  nand nand_20 (nand_20_out, old_state_0, old_state_0);
  nand nand_21 (nand_21_out, nand_1_out, nand_2_out);
  nand nand_22 (nand_22_out, nand_3_out, nand_4_out);
  nand nand_23 (nand_23_out, in_pressed, nand_5_out);
  nand nand_24 (nand_24_out, nand_6_out, old_state_1);
  nand nand_25 (nand_25_out, old_state_0, mode_on);
  nand nand_26 (nand_26_out, old_state_2, nand_7_out);
  nand nand_27 (nand_27_out, nand_8_out, old_state_0);
  nand nand_28 (nand_28_out, nand_9_out, old_state_1);
  nand nand_29 (nand_29_out, nand_10_out, mode_on);
  nand nand_30 (nand_30_out, nand_11_out, old_state_0);
  nand nand_31 (nand_31_out, nand_12_out, old_state_1);
  nand nand_32 (nand_32_out, nand_13_out, mode_on);
  nand nand_33 (nand_33_out, nand_14_out, nand_15_out);
  nand nand_34 (nand_34_out, old_state_2, nand_16_out);
  nand nand_35 (nand_35_out, nand_17_out, old_state_0);
  nand nand_36 (nand_36_out, nand_18_out, old_state_1);
  nand nand_37 (nand_37_out, nand_19_out, old_state_0);
  nand nand_38 (nand_38_out, old_state_2, old_state_1);
  nand nand_39 (nand_39_out, nand_20_out, mode_on);
  nand nand_40 (nand_40_out, nand_21_out, nand_21_out);
  nand nand_41 (nand_41_out, in_pressed, in_pressed);
  nand nand_42 (nand_42_out, nand_22_out, nand_22_out);
  nand nand_43 (nand_43_out, nand_23_out, nand_23_out);
  nand nand_44 (nand_44_out, nand_24_out, nand_24_out);
  nand nand_45 (nand_45_out, nand_25_out, nand_25_out);
  nand nand_46 (nand_46_out, nand_26_out, nand_26_out);
  nand nand_47 (nand_47_out, old_state_0, old_state_0);
  nand nand_48 (nand_48_out, in_pressed, in_pressed);
  nand nand_49 (nand_49_out, nand_27_out, nand_27_out);
  nand nand_50 (nand_50_out, nand_28_out, nand_28_out);
  nand nand_51 (nand_51_out, nand_29_out, nand_29_out);
  nand nand_52 (nand_52_out, old_state_2, old_state_2);
  nand nand_53 (nand_53_out, in_pressed, in_pressed);
  nand nand_54 (nand_54_out, nand_30_out, nand_30_out);
  nand nand_55 (nand_55_out, nand_31_out, nand_31_out);
  nand nand_56 (nand_56_out, nand_32_out, nand_32_out);
  nand nand_57 (nand_57_out, old_state_2, old_state_2);
  nand nand_58 (nand_58_out, in_pressed, in_pressed);
  nand nand_59 (nand_59_out, old_state_1, old_state_1);
  nand nand_60 (nand_60_out, old_state_0, old_state_0);
  nand nand_61 (nand_61_out, nand_33_out, nand_33_out);
  nand nand_62 (nand_62_out, in_pressed, in_pressed);
  nand nand_63 (nand_63_out, old_state_1, old_state_1);
  nand nand_64 (nand_64_out, old_state_0, old_state_0);
  nand nand_65 (nand_65_out, mode_on, mode_on);
  nand nand_66 (nand_66_out, mode_on, mode_on);
  nand nand_67 (nand_67_out, nand_34_out, nand_34_out);
  nand nand_68 (nand_68_out, old_state_0, old_state_0);
  nand nand_69 (nand_69_out, in_pressed, in_pressed);
  nand nand_70 (nand_70_out, nand_35_out, nand_35_out);
  nand nand_71 (nand_71_out, nand_36_out, nand_36_out);
  nand nand_72 (nand_72_out, in_pressed, in_pressed);
  nand nand_73 (nand_73_out, old_state_1, old_state_1);
  nand nand_74 (nand_74_out, old_state_0, old_state_0);
  nand nand_75 (nand_75_out, nand_37_out, nand_37_out);
  nand nand_76 (nand_76_out, in_pressed, in_pressed);
  nand nand_77 (nand_77_out, mode_on, mode_on);
  nand nand_78 (nand_78_out, nand_38_out, nand_38_out);
  nand nand_79 (nand_79_out, nand_39_out, nand_39_out);
  nand nand_80 (nand_80_out, nand_40_out, nand_41_out);
  nand nand_81 (nand_81_out, nand_42_out, nand_43_out);
  nand nand_82 (nand_82_out, old_state_1, in_pressed);
  nand nand_83 (nand_83_out, nand_44_out, nand_45_out);
  nand nand_84 (nand_84_out, nand_46_out, nand_47_out);
  nand nand_85 (nand_85_out, nand_48_out, mode_on);
  nand nand_86 (nand_86_out, nand_49_out, in_pressed);
  nand nand_87 (nand_87_out, nand_50_out, nand_51_out);
  nand nand_88 (nand_88_out, nand_52_out, old_state_1);
  nand nand_89 (nand_89_out, nand_53_out, mode_on);
  nand nand_90 (nand_90_out, nand_54_out, in_pressed);
  nand nand_91 (nand_91_out, nand_55_out, nand_56_out);
  nand nand_92 (nand_92_out, nand_57_out, old_state_1);
  nand nand_93 (nand_93_out, nand_58_out, mode_on);
  nand nand_94 (nand_94_out, nand_59_out, nand_60_out);
  nand nand_95 (nand_95_out, nand_61_out, old_state_0);
  nand nand_96 (nand_96_out, nand_62_out, mode_on);
  nand nand_97 (nand_97_out, old_state_1, old_state_0);
  nand nand_98 (nand_98_out, old_state_2, nand_63_out);
  nand nand_99 (nand_99_out, nand_64_out, mode_on);
  nand nand_100 (nand_100_out, old_state_0, nand_65_out);
  nand nand_101 (nand_101_out, old_state_1, nand_66_out);
  nand nand_102 (nand_102_out, old_state_1, old_state_0);
  nand nand_103 (nand_103_out, nand_67_out, nand_68_out);
  nand nand_104 (nand_104_out, nand_69_out, mode_on);
  nand nand_105 (nand_105_out, old_state_2, old_state_1);
  nand nand_106 (nand_106_out, nand_70_out, in_pressed);
  nand nand_107 (nand_107_out, nand_71_out, nand_72_out);
  nand nand_108 (nand_108_out, old_state_2, nand_73_out);
  nand nand_109 (nand_109_out, old_state_0, mode_on);
  nand nand_110 (nand_110_out, nand_74_out, in_pressed);
  nand nand_111 (nand_111_out, nand_75_out, nand_76_out);
  nand nand_112 (nand_112_out, old_state_0, nand_77_out);
  nand nand_113 (nand_113_out, nand_78_out, nand_79_out);
  nand nand_114 (nand_114_out, nand_80_out, mode_on);
  nand nand_115 (nand_115_out, old_state_0, old_state_0);
  nand nand_116 (nand_116_out, in_pressed, in_pressed);
  nand nand_117 (value_4, nand_81_out, nand_81_out);
  nand nand_118 (nand_118_out, nand_82_out, nand_83_out);
  nand nand_119 (nand_119_out, nand_84_out, nand_84_out);
  nand nand_120 (nand_120_out, nand_85_out, nand_85_out);
  nand nand_121 (nand_121_out, nand_86_out, nand_87_out);
  nand nand_122 (nand_122_out, nand_88_out, nand_88_out);
  nand nand_123 (nand_123_out, nand_89_out, nand_89_out);
  nand nand_124 (nand_124_out, nand_90_out, nand_91_out);
  nand nand_125 (nand_125_out, nand_92_out, nand_92_out);
  nand nand_126 (nand_126_out, nand_93_out, nand_93_out);
  nand nand_127 (nand_127_out, nand_94_out, nand_94_out);
  nand nand_128 (nand_128_out, nand_95_out, nand_95_out);
  nand nand_129 (nand_129_out, nand_96_out, nand_96_out);
  nand nand_130 (nand_130_out, nand_97_out, nand_97_out);
  nand nand_131 (nand_131_out, nand_98_out, nand_98_out);
  nand nand_132 (nand_132_out, nand_99_out, nand_99_out);
  nand nand_133 (nand_133_out, nand_100_out, nand_101_out);
  nand nand_134 (nand_134_out, nand_102_out, nand_102_out);
  nand nand_135 (nand_135_out, nand_103_out, nand_103_out);
  nand nand_136 (nand_136_out, nand_104_out, nand_104_out);
  nand nand_137 (nand_137_out, nand_105_out, nand_105_out);
  nand nand_138 (nand_138_out, nand_106_out, nand_107_out);
  nand nand_139 (nand_139_out, old_state_0, old_state_0);
  nand nand_140 (nand_140_out, mode_on, mode_on);
  nand nand_141 (nand_141_out, nand_108_out, nand_108_out);
  nand nand_142 (nand_142_out, nand_109_out, nand_109_out);
  nand nand_143 (nand_143_out, nand_110_out, nand_111_out);
  nand nand_144 (nand_144_out, nand_112_out, nand_113_out);
  nand nand_145 (nand_145_out, nand_114_out, nand_114_out);
  nand nand_146 (nand_146_out, nand_115_out, in_pressed);
  nand nand_147 (nand_147_out, old_state_0, nand_116_out);
  nand nand_148 (nand_148_out, old_state_2, old_state_1);
  nand nand_149 (nand_149_out, nand_118_out, nand_118_out);
  nand nand_150 (nand_150_out, nand_119_out, nand_120_out);
  nand nand_151 (nand_151_out, nand_121_out, nand_121_out);
  nand nand_152 (nand_152_out, nand_122_out, nand_123_out);
  nand nand_153 (nand_153_out, nand_124_out, nand_124_out);
  nand nand_154 (nand_154_out, nand_125_out, nand_126_out);
  nand nand_155 (nand_155_out, nand_127_out, in_pressed);
  nand nand_156 (nand_156_out, nand_128_out, nand_129_out);
  nand nand_157 (nand_157_out, nand_130_out, in_pressed);
  nand nand_158 (nand_158_out, nand_131_out, nand_132_out);
  nand nand_159 (nand_159_out, nand_133_out, nand_133_out);
  nand nand_160 (nand_160_out, nand_134_out, in_pressed);
  nand nand_161 (nand_161_out, nand_135_out, nand_136_out);
  nand nand_162 (nand_162_out, nand_137_out, old_state_0);
  nand nand_163 (nand_163_out, nand_138_out, nand_138_out);
  nand nand_164 (nand_164_out, old_state_1, nand_139_out);
  nand nand_165 (nand_165_out, old_state_1, nand_140_out);
  nand nand_166 (nand_166_out, nand_141_out, nand_142_out);
  nand nand_167 (nand_167_out, nand_143_out, nand_143_out);
  nand nand_168 (nand_168_out, nand_144_out, nand_144_out);
  nand nand_169 (nand_169_out, nand_145_out, nand_146_out);
  nand nand_170 (nand_170_out, nand_147_out, nand_148_out);
  nand nand_171 (value_3, nand_149_out, nand_150_out);
  nand nand_172 (value_2, nand_151_out, nand_152_out);
  nand nand_173 (value_1, nand_153_out, nand_154_out);
  nand nand_174 (nand_174_out, nand_155_out, nand_156_out);
  nand nand_175 (nand_175_out, nand_157_out, nand_158_out);
  nand nand_176 (nand_176_out, nand_159_out, nand_160_out);
  nand nand_177 (nand_177_out, nand_161_out, nand_162_out);
  nand nand_178 (nand_178_out, nand_163_out, nand_164_out);
  nand nand_179 (nand_179_out, nand_165_out, nand_166_out);
  nand nand_180 (S_0, nand_167_out, nand_168_out);
  nand nand_181 (nand_181_out, nand_169_out, nand_169_out);
  nand nand_182 (nand_182_out, nand_170_out, nand_170_out);
  nand nand_183 (nand_183_out, nand_174_out, nand_174_out);
  nand nand_184 (nand_184_out, nand_175_out, nand_175_out);
  nand nand_185 (nand_185_out, nand_176_out, nand_176_out);
  nand nand_186 (nand_186_out, nand_177_out, nand_177_out);
  nand nand_187 (nand_187_out, nand_178_out, nand_178_out);
  nand nand_188 (nand_188_out, nand_179_out, nand_179_out);
  nand nand_189 (sign, nand_181_out, nand_182_out);
  nand nand_190 (value_0, nand_183_out, nand_184_out);
  nand nand_191 (S_2, nand_185_out, nand_186_out);
  nand nand_192 (S_1, nand_187_out, nand_188_out);

  assign value_5 = 1'b0;
endmodule

module jukebox (
  input  [3:0] mode_on,
  input  [11:0] input_bus,
  input  R,
  output [29:0] O_text,
  output [1:0] O_music,
  output set_music_on
);

  wire and_1_out;
  wire [1:0] counter_1_q;
  wire [4:0] undriven, undriven_2, undriven_3, undriven_4, undriven_5, undriven_6, undriven_7, undriven_8,
       undriven_9, undriven_10, undriven_11, undriven_12;

  Comparator #(.width(4)) comparator_1 (.a(mode_on), .b(4'b1001), .eq(set_music_on));  // open: gt, lt
  and and_1 (and_1_out, set_music_on, input_bus[11]);
  Counter #(.width(2), .max('h1)) counter_1 (
    .clr(R), .load(1'b0), .up(1'b1), .count(1'b1), .clk(and_1_out), .D(2'b00), .Q(counter_1_q));  // open: carry
  Multiplexer #(.select(2), .width(30), .enable("false")) multiplexer_1 (
    .in0(30'h338ef5db), .in1(30'h37f10c1f),
    .in2({undriven_6, undriven_5, undriven_4, undriven_3, undriven_2, undriven}),
    .in3({undriven_12, undriven_11, undriven_10, undriven_9, undriven_8, undriven_7}), .out(O_text),
    .sel(counter_1_q));
  Multiplexer #(.width(2), .enable("false")) multiplexer_2 (
    .in0(2'b00), .in1(counter_1_q), .out(O_music), .sel(set_music_on));
endmodule

module set_time_zone_2 (
  input  [29:0] time_bus,
  input  [11:0] input_bus,
  input  [3:0] mode_on,
  input  R,
  output [29:0] time_outpus,
  output [29:0] out_6
);

  Multiplexer #(.select(2), .width(30), .enable("false")) multiplexer_1 (
    .in0(30'h2b8bb717), .in1(30'h2aaf73ff), .in2(30'h2b8bf775), .in3(30'h31c5295f), .out(out_6));  // open: sel
  set_time_to_23 set_time_to_23_1 (
    .R(R), .I_1(time_bus[29:25]), .I_0(time_bus[24:20]), .O_1(time_outpus[29:25]), .O_0(time_outpus[24:20]));  // open: B_1, B_0, load, set_on

  assign time_outpus[19:0] = time_bus[19:0];
endmodule

module chrono (
  input  [11:0] input_bus,
  input  [3:0] mode_on,
  input  R,
  output [29:0] O_0
);

  wire and_1_out, clock_1_out, clock_2_out, comparator_1_eq, comparator_2_eq, comparator_3_eq, not_1_out,
       or_1_out, t_ff_1_q;
  wire [5:0] binary_to_time_converter_1_output_bus_1, binary_to_time_converter_2_output_bus_1,
       binary_to_time_converter_3_output_bus_1, counter_1_q, counter_2_q, counter_3_q;

  Clock #(.highDuration(1000000), .lowDuration(1000000)) clock_1 (.out(clock_1_out));
  T_Flip_Flop t_ff_1 (.T(input_bus[11]), .clk(clock_2_out), .Q(t_ff_1_q));  // open: Qn, reset, preset
  Clock #(.highDuration(2), .lowDuration(2)) clock_2 (.out(clock_2_out));
  Comparator #(.width(4)) comparator_1 (.a(mode_on), .b(4'b1011), .eq(comparator_1_eq));  // open: gt, lt
  not not_1 (not_1_out, comparator_1_eq);
  or or_1 (or_1_out, not_1_out, R);
  binary_to_time_converter binary_to_time_converter_1 (
    .Input_bus_1({5{1'b0}}), .Input_bus_2({5{1'b0}}), .Output_bus_1(binary_to_time_converter_1_output_bus_1));
  binary_to_time_converter binary_to_time_converter_2 (
    .Input_bus_1({5{1'b0}}), .Input_bus_2({5{1'b0}}), .Output_bus_1(binary_to_time_converter_2_output_bus_1));
  binary_to_time_converter binary_to_time_converter_3 (
    .Input_bus_1({5{1'b0}}), .Input_bus_2({5{1'b0}}), .Output_bus_1(binary_to_time_converter_3_output_bus_1));
  Counter #(.width(6), .max('h17)) counter_1 (
    .clr(or_1_out), .load(1'b0), .up(1'b1), .count(and_1_out), .clk(clock_1_out),
    .D(binary_to_time_converter_1_output_bus_1), .Q(counter_1_q));  // open: carry
  Counter #(.width(6), .max('h3b)) counter_2 (
    .clr(or_1_out), .load(1'b0), .up(1'b1), .count(comparator_3_eq), .clk(clock_1_out),
    .D(binary_to_time_converter_2_output_bus_1), .Q(counter_2_q));  // open: carry
  Counter #(.width(6), .max('h3b)) counter_3 (
    .clr(or_1_out), .load(1'b0), .up(1'b1), .count(t_ff_1_q), .clk(clock_1_out),
    .D(binary_to_time_converter_3_output_bus_1), .Q(counter_3_q));  // open: carry
  Comparator #(.width(6)) comparator_2 (.a(6'b111011), .b(counter_2_q), .eq(comparator_2_eq));  // open: gt, lt
  Comparator #(.width(6)) comparator_3 (.a(6'b111011), .b(counter_3_q), .eq(comparator_3_eq));  // open: gt, lt
  and and_1 (and_1_out, comparator_2_eq, comparator_3_eq);
  time_to_binary_converter time_to_binary_converter_1 (.t_in(counter_1_q), .O_1(O_0[29:25]), .O_0(O_0[24:20]));
  time_to_binary_converter time_to_binary_converter_2 (.t_in(counter_2_q), .O_1(O_0[19:15]), .O_0(O_0[14:10]));
  time_to_binary_converter time_to_binary_converter_3 (.t_in(counter_3_q), .O_1(O_0[9:5]), .O_0(O_0[4:0]));
endmodule
